// Digital circuit BadApple.dig as structural Verilog
module BadApple (
  input  clk,
  output [7:0] out_2,
  output [3:0] out_3,
  output [15:0] out_4,
  output [7:0] out_5,
  output [7:0] out_6,
  output [7:0] out_7,
  output [7:0] out_8,
  output [7:0] out_9,
  output [15:0] out_10,
  output [7:0] out_11,
  output [3:0] out_12,
  output [7:0] out_13
);

  wire add_1_c_o, ADO, AI, AO, BI, BO, CARO, CI, CLK_t, CLR, CLR1, CLR2, CO, CO1, CO2, COE, COE1, COE2,
       counter_1_ovf, counter_3_ovf, decoder_1_out_2, decoder_1_out_3, decoder_1_out_4, decoder_1_out_5,
       decoder_1_out_6, decoder_1_out_7, decoder_1_out_8, decoder_1_out_9, decoder_1_out_10,
       decoder_1_out_11, decoder_1_out_12, decoder_1_out_13, decoder_1_out_14, decoder_1_out_15,
       demultiplexer_1_out_0, demultiplexer_1_out_1, demultiplexer_1_out_2, demultiplexer_1_out_3,
       demultiplexer_1_out_4, demultiplexer_1_out_5, demultiplexer_1_out_6, demultiplexer_1_out_7,
       demultiplexer_1_out_8, demultiplexer_1_out_9, demultiplexer_1_out_10, demultiplexer_1_out_11,
       demultiplexer_1_out_12, demultiplexer_1_out_13, demultiplexer_1_out_14, demultiplexer_1_out_15,
       demultiplexer_3_out_0, demultiplexer_3_out_1, demultiplexer_3_out_2, demultiplexer_3_out_3,
       demultiplexer_3_out_4, demultiplexer_3_out_5, demultiplexer_3_out_6, FI, HBI, HLT, IRI, IRI2, LBI,
       MAR, MI, MRI, MRI2, nor_1_out, NXT, or_1_out, or_2_out, OUT, pulldown_2_out, pullup_2_out,
       pullup_3_out, RAO, RAO2, rs_ff_as_1_q, SAO, SUB;
  wire [1:0] comparator_1_lt, driver_6_out, driver_8_out;
  wire [2:0] counter_2_out;
  wire [3:0] counter_1_out;
  wire [7:0] pulldown_4_out, xor_1_out;
  wire [7:4] register_21_q;
  wire [11:0] CW;
  wire [14:14] rom_7_d;
  wire [15:0] and_1_out, and_2_out, and_3_out, and_4_out, and_5_out, and_6_out, and_7_out, and_8_out,
       and_9_out, and_10_out, and_11_out, and_12_out, and_13_out, and_14_out, and_15_out, and_16_out,
       demultiplexer_2_out_0, demultiplexer_2_out_1, demultiplexer_2_out_2, demultiplexer_2_out_3,
       demultiplexer_2_out_4, demultiplexer_2_out_5, demultiplexer_2_out_6, demultiplexer_2_out_7,
       demultiplexer_2_out_8, demultiplexer_2_out_9, demultiplexer_2_out_10, demultiplexer_2_out_11,
       demultiplexer_2_out_12, demultiplexer_2_out_13, demultiplexer_2_out_14, demultiplexer_2_out_15,
       driver_1_out, driverinvsel_1_out, pullup_1_out, register_1_q, register_2_q, register_3_q,
       register_4_q, register_5_q, register_6_q, register_7_q, register_8_q, register_9_q, register_10_q,
       register_11_q, register_12_q, register_13_q, register_14_q, register_15_q, register_16_q;

  Demultiplexer #(.Selector_Bits(4)) demultiplexer_1 (
    .sel(counter_1_out), .in(MI), .out_0(demultiplexer_1_out_0), .out_1(demultiplexer_1_out_1),
    .out_2(demultiplexer_1_out_2), .out_3(demultiplexer_1_out_3), .out_4(demultiplexer_1_out_4),
    .out_5(demultiplexer_1_out_5), .out_6(demultiplexer_1_out_6), .out_7(demultiplexer_1_out_7),
    .out_8(demultiplexer_1_out_8), .out_9(demultiplexer_1_out_9), .out_10(demultiplexer_1_out_10),
    .out_11(demultiplexer_1_out_11), .out_12(demultiplexer_1_out_12), .out_13(demultiplexer_1_out_13),
    .out_14(demultiplexer_1_out_14), .out_15(demultiplexer_1_out_15));
  Register #(.Bits(16)) register_1 (.D(and_4_out), .C(CLK_t), .en(demultiplexer_1_out_0), .Q(register_1_q));
  Counter #(.Bits(4)) counter_1 (.en(MI), .C(CLK_t), .clr(or_1_out), .out(counter_1_out), .ovf(counter_1_ovf));
  Register #(.Bits(16)) register_2 (.D(and_3_out), .C(CLK_t), .en(demultiplexer_1_out_1), .Q(register_2_q));
  LED led_1 (.in(register_1_q[15]));
  LED led_2 (.in(register_1_q[14]));
  LED led_3 (.in(register_2_q[15]));
  LED led_4 (.in(register_2_q[14]));
  LED led_5 (.in(register_3_q[15]));
  LED led_6 (.in(register_3_q[14]));
  LED led_7 (.in(register_5_q[15]));
  LED led_8 (.in(register_5_q[14]));
  LED led_9 (.in(register_4_q[15]));
  LED led_10 (.in(register_4_q[14]));
  LED led_11 (.in(register_6_q[15]));
  LED led_12 (.in(register_6_q[14]));
  LED led_13 (.in(register_7_q[15]));
  LED led_14 (.in(register_7_q[14]));
  LED led_15 (.in(register_8_q[15]));
  LED led_16 (.in(register_8_q[14]));
  LED led_17 (.in(register_9_q[15]));
  LED led_18 (.in(register_9_q[14]));
  LED led_19 (.in(register_10_q[15]));
  LED led_20 (.in(register_10_q[14]));
  LED led_21 (.in(register_11_q[15]));
  LED led_22 (.in(register_11_q[14]));
  LED led_23 (.in(register_13_q[15]));
  LED led_24 (.in(register_13_q[14]));
  LED led_25 (.in(register_12_q[15]));
  LED led_26 (.in(register_12_q[14]));
  LED led_27 (.in(register_14_q[15]));
  LED led_28 (.in(register_14_q[14]));
  LED led_29 (.in(register_15_q[15]));
  LED led_30 (.in(register_15_q[14]));
  LED led_31 (.in(register_16_q[15]));
  LED led_32 (.in(register_16_q[14]));
  or or_1 (or_1_out, MAR, counter_1_ovf);
  Register #(.Bits(16)) register_3 (.D(and_2_out), .C(CLK_t), .en(demultiplexer_1_out_2), .Q(register_3_q));
  LED led_33 (.in(register_1_q[13]));
  LED led_34 (.in(register_1_q[12]));
  LED led_35 (.in(register_2_q[13]));
  LED led_36 (.in(register_2_q[12]));
  LED led_37 (.in(register_3_q[13]));
  LED led_38 (.in(register_3_q[12]));
  LED led_39 (.in(register_5_q[13]));
  LED led_40 (.in(register_5_q[12]));
  LED led_41 (.in(register_4_q[13]));
  LED led_42 (.in(register_4_q[12]));
  LED led_43 (.in(register_6_q[13]));
  LED led_44 (.in(register_6_q[12]));
  LED led_45 (.in(register_7_q[13]));
  LED led_46 (.in(register_7_q[12]));
  LED led_47 (.in(register_8_q[13]));
  LED led_48 (.in(register_8_q[12]));
  LED led_49 (.in(register_9_q[13]));
  LED led_50 (.in(register_9_q[12]));
  LED led_51 (.in(register_10_q[13]));
  LED led_52 (.in(register_10_q[12]));
  LED led_53 (.in(register_11_q[13]));
  LED led_54 (.in(register_11_q[12]));
  LED led_55 (.in(register_13_q[13]));
  LED led_56 (.in(register_13_q[12]));
  LED led_57 (.in(register_12_q[13]));
  LED led_58 (.in(register_12_q[12]));
  LED led_59 (.in(register_14_q[13]));
  LED led_60 (.in(register_14_q[12]));
  LED led_61 (.in(register_15_q[13]));
  LED led_62 (.in(register_15_q[12]));
  LED led_63 (.in(register_16_q[13]));
  LED led_64 (.in(register_16_q[12]));
  assign and_1_out = demultiplexer_2_out_3 & driver_1_out;  // And and_1, 16 bits wide
  assign and_2_out = demultiplexer_2_out_2 & driver_1_out;  // And and_2, 16 bits wide
  assign and_3_out = demultiplexer_2_out_1 & driver_1_out;  // And and_3, 16 bits wide
  assign and_4_out = demultiplexer_2_out_0 & driver_1_out;  // And and_4, 16 bits wide
  Demultiplexer #(.Selector_Bits(4), .Bits(16)) demultiplexer_2 (
    .sel(counter_1_out), .in(pullup_1_out), .out_0(demultiplexer_2_out_0), .out_1(demultiplexer_2_out_1),
    .out_2(demultiplexer_2_out_2), .out_3(demultiplexer_2_out_3), .out_4(demultiplexer_2_out_4),
    .out_5(demultiplexer_2_out_5), .out_6(demultiplexer_2_out_6), .out_7(demultiplexer_2_out_7),
    .out_8(demultiplexer_2_out_8), .out_9(demultiplexer_2_out_9), .out_10(demultiplexer_2_out_10),
    .out_11(demultiplexer_2_out_11), .out_12(demultiplexer_2_out_12), .out_13(demultiplexer_2_out_13),
    .out_14(demultiplexer_2_out_14), .out_15(demultiplexer_2_out_15));
  Register #(.Bits(16)) register_4 (.D(and_8_out), .C(CLK_t), .en(demultiplexer_1_out_4), .Q(register_4_q));
  Register #(.Bits(16)) register_5 (.D(and_1_out), .C(CLK_t), .en(demultiplexer_1_out_3), .Q(register_5_q));
  LED led_65 (.in(register_1_q[11]));
  LED led_66 (.in(register_1_q[10]));
  LED led_67 (.in(register_2_q[11]));
  LED led_68 (.in(register_2_q[10]));
  LED led_69 (.in(register_3_q[11]));
  LED led_70 (.in(register_3_q[10]));
  LED led_71 (.in(register_5_q[11]));
  LED led_72 (.in(register_5_q[10]));
  LED led_73 (.in(register_4_q[11]));
  LED led_74 (.in(register_4_q[10]));
  LED led_75 (.in(register_6_q[11]));
  LED led_76 (.in(register_6_q[10]));
  LED led_77 (.in(register_7_q[11]));
  LED led_78 (.in(register_7_q[10]));
  LED led_79 (.in(register_8_q[11]));
  LED led_80 (.in(register_8_q[10]));
  LED led_81 (.in(register_9_q[11]));
  LED led_82 (.in(register_9_q[10]));
  LED led_83 (.in(register_10_q[11]));
  LED led_84 (.in(register_10_q[10]));
  LED led_85 (.in(register_11_q[11]));
  LED led_86 (.in(register_11_q[10]));
  LED led_87 (.in(register_13_q[11]));
  LED led_88 (.in(register_13_q[10]));
  LED led_89 (.in(register_12_q[11]));
  LED led_90 (.in(register_12_q[10]));
  LED led_91 (.in(register_14_q[11]));
  LED led_92 (.in(register_14_q[10]));
  LED led_93 (.in(register_15_q[11]));
  LED led_94 (.in(register_15_q[10]));
  LED led_95 (.in(register_16_q[11]));
  LED led_96 (.in(register_16_q[10]));
  Register #(.Bits(16)) register_6 (.D(and_7_out), .C(CLK_t), .en(demultiplexer_1_out_5), .Q(register_6_q));
  LED led_97 (.in(register_1_q[9]));
  LED led_98 (.in(register_1_q[8]));
  LED led_99 (.in(register_2_q[9]));
  LED led_100 (.in(register_2_q[8]));
  LED led_101 (.in(register_3_q[9]));
  LED led_102 (.in(register_3_q[8]));
  LED led_103 (.in(register_5_q[9]));
  LED led_104 (.in(register_5_q[8]));
  LED led_105 (.in(register_4_q[9]));
  LED led_106 (.in(register_4_q[8]));
  LED led_107 (.in(register_6_q[9]));
  LED led_108 (.in(register_6_q[8]));
  LED led_109 (.in(register_7_q[9]));
  LED led_110 (.in(register_7_q[8]));
  LED led_111 (.in(register_8_q[9]));
  LED led_112 (.in(register_8_q[8]));
  LED led_113 (.in(register_9_q[9]));
  LED led_114 (.in(register_9_q[8]));
  LED led_115 (.in(register_10_q[9]));
  LED led_116 (.in(register_10_q[8]));
  LED led_117 (.in(register_11_q[9]));
  LED led_118 (.in(register_11_q[8]));
  LED led_119 (.in(register_13_q[9]));
  LED led_120 (.in(register_13_q[8]));
  LED led_121 (.in(register_12_q[9]));
  LED led_122 (.in(register_12_q[8]));
  LED led_123 (.in(register_14_q[9]));
  LED led_124 (.in(register_14_q[8]));
  LED led_125 (.in(register_15_q[9]));
  LED led_126 (.in(register_15_q[8]));
  LED led_127 (.in(register_16_q[9]));
  LED led_128 (.in(register_16_q[8]));
  PullUp #(.Bits(16)) pullup_1 (.out(pullup_1_out));
  Register #(.Bits(16)) register_7 (.D(and_6_out), .C(CLK_t), .en(demultiplexer_1_out_6), .Q(register_7_q));
  LED led_129 (.in(register_1_q[7]));
  LED led_130 (.in(register_1_q[6]));
  LED led_131 (.in(register_2_q[7]));
  LED led_132 (.in(register_2_q[6]));
  LED led_133 (.in(register_3_q[7]));
  LED led_134 (.in(register_3_q[6]));
  LED led_135 (.in(register_5_q[7]));
  LED led_136 (.in(register_5_q[6]));
  LED led_137 (.in(register_4_q[7]));
  LED led_138 (.in(register_4_q[6]));
  LED led_139 (.in(register_6_q[7]));
  LED led_140 (.in(register_6_q[6]));
  LED led_141 (.in(register_7_q[7]));
  LED led_142 (.in(register_7_q[6]));
  LED led_143 (.in(register_8_q[7]));
  LED led_144 (.in(register_8_q[6]));
  LED led_145 (.in(register_9_q[7]));
  LED led_146 (.in(register_9_q[6]));
  LED led_147 (.in(register_10_q[7]));
  LED led_148 (.in(register_10_q[6]));
  LED led_149 (.in(register_11_q[7]));
  LED led_150 (.in(register_11_q[6]));
  LED led_151 (.in(register_13_q[7]));
  LED led_152 (.in(register_13_q[6]));
  LED led_153 (.in(register_12_q[7]));
  LED led_154 (.in(register_12_q[6]));
  LED led_155 (.in(register_14_q[7]));
  LED led_156 (.in(register_14_q[6]));
  LED led_157 (.in(register_15_q[7]));
  LED led_158 (.in(register_15_q[6]));
  LED led_159 (.in(register_16_q[7]));
  LED led_160 (.in(register_16_q[6]));
  assign and_5_out = demultiplexer_2_out_7 & driver_1_out;  // And and_5, 16 bits wide
  assign and_6_out = demultiplexer_2_out_6 & driver_1_out;  // And and_6, 16 bits wide
  assign and_7_out = demultiplexer_2_out_5 & driver_1_out;  // And and_7, 16 bits wide
  assign and_8_out = demultiplexer_2_out_4 & driver_1_out;  // And and_8, 16 bits wide
  Register #(.Bits(16)) register_8 (.D(and_5_out), .C(CLK_t), .en(demultiplexer_1_out_7), .Q(register_8_q));
  Register #(.Bits(16)) register_9 (.D(and_12_out), .C(CLK_t), .en(demultiplexer_1_out_8), .Q(register_9_q));
  LED led_161 (.in(register_1_q[5]));
  LED led_162 (.in(register_1_q[4]));
  LED led_163 (.in(register_2_q[5]));
  LED led_164 (.in(register_2_q[4]));
  LED led_165 (.in(register_3_q[5]));
  LED led_166 (.in(register_3_q[4]));
  LED led_167 (.in(register_5_q[5]));
  LED led_168 (.in(register_5_q[4]));
  LED led_169 (.in(register_4_q[5]));
  LED led_170 (.in(register_4_q[4]));
  LED led_171 (.in(register_6_q[5]));
  LED led_172 (.in(register_6_q[4]));
  LED led_173 (.in(register_7_q[5]));
  LED led_174 (.in(register_7_q[4]));
  LED led_175 (.in(register_8_q[5]));
  LED led_176 (.in(register_8_q[4]));
  LED led_177 (.in(register_9_q[5]));
  LED led_178 (.in(register_9_q[4]));
  LED led_179 (.in(register_10_q[5]));
  LED led_180 (.in(register_10_q[4]));
  LED led_181 (.in(register_11_q[5]));
  LED led_182 (.in(register_11_q[4]));
  LED led_183 (.in(register_13_q[5]));
  LED led_184 (.in(register_13_q[4]));
  LED led_185 (.in(register_12_q[5]));
  LED led_186 (.in(register_12_q[4]));
  LED led_187 (.in(register_14_q[5]));
  LED led_188 (.in(register_14_q[4]));
  LED led_189 (.in(register_15_q[5]));
  LED led_190 (.in(register_15_q[4]));
  LED led_191 (.in(register_16_q[5]));
  LED led_192 (.in(register_16_q[4]));
  Register #(.Bits(16)) register_10 (.D(and_11_out), .C(CLK_t), .en(demultiplexer_1_out_9), .Q(register_10_q));
  LED led_193 (.in(register_1_q[3]));
  LED led_194 (.in(register_1_q[2]));
  LED led_195 (.in(register_2_q[3]));
  LED led_196 (.in(register_2_q[2]));
  LED led_197 (.in(register_3_q[3]));
  LED led_198 (.in(register_3_q[2]));
  LED led_199 (.in(register_5_q[3]));
  LED led_200 (.in(register_5_q[2]));
  LED led_201 (.in(register_4_q[3]));
  LED led_202 (.in(register_4_q[2]));
  LED led_203 (.in(register_6_q[3]));
  LED led_204 (.in(register_6_q[2]));
  LED led_205 (.in(register_7_q[3]));
  LED led_206 (.in(register_7_q[2]));
  LED led_207 (.in(register_8_q[3]));
  LED led_208 (.in(register_8_q[2]));
  LED led_209 (.in(register_9_q[3]));
  LED led_210 (.in(register_9_q[2]));
  LED led_211 (.in(register_10_q[3]));
  LED led_212 (.in(register_10_q[2]));
  LED led_213 (.in(register_11_q[3]));
  LED led_214 (.in(register_11_q[2]));
  LED led_215 (.in(register_13_q[3]));
  LED led_216 (.in(register_13_q[2]));
  LED led_217 (.in(register_12_q[3]));
  LED led_218 (.in(register_12_q[2]));
  LED led_219 (.in(register_14_q[3]));
  LED led_220 (.in(register_14_q[2]));
  LED led_221 (.in(register_15_q[3]));
  LED led_222 (.in(register_15_q[2]));
  LED led_223 (.in(register_16_q[3]));
  LED led_224 (.in(register_16_q[2]));
  Register #(.Bits(16)) register_11 (.D(and_10_out), .C(CLK_t), .en(demultiplexer_1_out_10), .Q(register_11_q));
  LED led_225 (.in(register_1_q[1]));
  LED led_226 (.in(register_1_q[0]));
  LED led_227 (.in(register_2_q[1]));
  LED led_228 (.in(register_2_q[0]));
  LED led_229 (.in(register_3_q[1]));
  LED led_230 (.in(register_3_q[0]));
  LED led_231 (.in(register_5_q[1]));
  LED led_232 (.in(register_5_q[0]));
  LED led_233 (.in(register_4_q[1]));
  LED led_234 (.in(register_4_q[0]));
  LED led_235 (.in(register_6_q[1]));
  LED led_236 (.in(register_6_q[0]));
  LED led_237 (.in(register_7_q[1]));
  LED led_238 (.in(register_7_q[0]));
  LED led_239 (.in(register_8_q[1]));
  LED led_240 (.in(register_8_q[0]));
  LED led_241 (.in(register_9_q[1]));
  LED led_242 (.in(register_9_q[0]));
  LED led_243 (.in(register_10_q[1]));
  LED led_244 (.in(register_10_q[0]));
  LED led_245 (.in(register_11_q[1]));
  LED led_246 (.in(register_11_q[0]));
  LED led_247 (.in(register_13_q[1]));
  LED led_248 (.in(register_13_q[0]));
  LED led_249 (.in(register_12_q[1]));
  LED led_250 (.in(register_12_q[0]));
  LED led_251 (.in(register_14_q[1]));
  LED led_252 (.in(register_14_q[0]));
  LED led_253 (.in(register_15_q[1]));
  LED led_254 (.in(register_15_q[0]));
  LED led_255 (.in(register_16_q[1]));
  LED led_256 (.in(register_16_q[0]));
  assign and_9_out = demultiplexer_2_out_11 & driver_1_out;  // And and_9, 16 bits wide
  assign and_10_out = demultiplexer_2_out_10 & driver_1_out;  // And and_10, 16 bits wide
  assign and_11_out = demultiplexer_2_out_9 & driver_1_out;  // And and_11, 16 bits wide
  assign and_12_out = demultiplexer_2_out_8 & driver_1_out;  // And and_12, 16 bits wide
  Register #(.Bits(16)) register_12 (.D(and_16_out), .C(CLK_t), .en(demultiplexer_1_out_12), .Q(register_12_q));
  Register #(.Bits(16)) register_13 (.D(and_9_out), .C(CLK_t), .en(demultiplexer_1_out_11), .Q(register_13_q));
  Register #(.Bits(16)) register_14 (.D(and_15_out), .C(CLK_t), .en(demultiplexer_1_out_13), .Q(register_14_q));
  Register #(.Bits(16)) register_15 (.D(and_14_out), .C(CLK_t), .en(demultiplexer_1_out_14), .Q(register_15_q));
  assign and_13_out = demultiplexer_2_out_15 & driver_1_out;  // And and_13, 16 bits wide
  assign and_14_out = demultiplexer_2_out_14 & driver_1_out;  // And and_14, 16 bits wide
  assign and_15_out = demultiplexer_2_out_13 & driver_1_out;  // And and_15, 16 bits wide
  assign and_16_out = demultiplexer_2_out_12 & driver_1_out;  // And and_16, 16 bits wide
  Register #(.Bits(16)) register_16 (.D(and_13_out), .C(CLK_t), .en(demultiplexer_1_out_15), .Q(register_16_q));
  assign driver_1_out = MI ? driverinvsel_1_out : 16'bz;  // Driver driver_1
  PullDown #(.Bits(16)) pulldown_1 (.out(driver_1_out));
  RS_FF_AS rs_ff_as_1 (.S(HLT), .R(CLR), .Q(rs_ff_as_1_q));  // open: nQ
  LED led_257 (.in(out_8[7]));
  LED led_258 (.in(out_7[7]));
  LED led_259 (.in(out_5[7]));
  LED led_260 (.in(out_2[7]));
  LED led_261 (.in(out_8[3]));
  LED led_262 (.in(out_8[4]));
  LED led_263 (.in(out_8[5]));
  LED led_264 (.in(out_8[6]));
  LED led_265 (.in(out_7[3]));
  LED led_266 (.in(out_7[4]));
  LED led_267 (.in(out_7[5]));
  LED led_268 (.in(out_7[6]));
  LED led_269 (.in(out_5[3]));
  LED led_270 (.in(out_5[4]));
  LED led_271 (.in(out_5[5]));
  LED led_272 (.in(out_5[6]));
  LED led_273 (.in(out_2[3]));
  LED led_274 (.in(out_2[4]));
  LED led_275 (.in(out_2[5]));
  LED led_276 (.in(out_2[6]));
  CounterPreset #(.Bits(16)) counterpreset_1 (
    .en(COE), .C(CLK_t), .dir(pulldown_2_out), .in(driverinvsel_1_out), .ld(CI), .clr(CLR2), .out(out_4),
    .ovf(CLR1));
  PullDown pulldown_2 (.out(pulldown_2_out));
  assign driverinvsel_1_out = ~CO ? {out_7, out_6} : 16'bz;  // DriverInvSel driverinvsel_1
  Register #(.Bits(16)) register_17 (.D(driverinvsel_1_out), .C(CLK_t), .en(MRI), .Q(out_10));
  Demultiplexer #(.Selector_Bits(3)) demultiplexer_3 (
    .sel(counter_2_out), .in(RAO), .out_0(demultiplexer_3_out_0), .out_1(demultiplexer_3_out_1),
    .out_2(demultiplexer_3_out_2), .out_3(demultiplexer_3_out_3), .out_4(demultiplexer_3_out_4),
    .out_5(demultiplexer_3_out_5), .out_6(demultiplexer_3_out_6));  // open: out_7
  and and_17 (CLK_t, clk, ~rs_ff_as_1_q);  // And
  LED led_277 (.in(out_8[0]));
  LED led_278 (.in(out_8[1]));
  LED led_279 (.in(out_8[2]));
  LED led_280 (.in(out_7[0]));
  LED led_281 (.in(out_7[1]));
  LED led_282 (.in(out_7[2]));
  LED led_283 (.in(out_5[0]));
  LED led_284 (.in(out_5[1]));
  LED led_285 (.in(out_5[2]));
  LED led_286 (.in(out_2[0]));
  LED led_287 (.in(out_2[1]));
  LED led_288 (.in(out_2[2]));
  assign driverinvsel_1_out = CO ? out_4 : 16'bz;  // Driver driver_2
  Counter #(.Bits(3)) counter_2 (.en(CLR1), .C(CLK_t), .clr(demultiplexer_3_out_6), .out(counter_2_out));  // open: ovf
  LED led_289 (.in(out_9[4]));
  LED led_290 (.in(out_9[5]));
  LED led_291 (.in(out_9[6]));
  LED led_292 (.in(out_9[7]));
  LED led_293 (.in(out_6[4]));
  LED led_294 (.in(out_6[5]));
  LED led_295 (.in(out_6[6]));
  LED led_296 (.in(out_6[7]));
  LED led_297 (.in(decoder_1_out_15));
  LED led_298 (.in(decoder_1_out_14));
  Register #(.Bits(8)) register_18 (.D(out_11), .C(CLK_t), .en(HBI), .Q(out_7));
  Register #(.Bits(8)) register_19 (.D(out_11), .C(CLK_t), .en(LBI), .Q(out_6));
  ROM #(.AddrBits(16), .Bits(8)) rom_1 (.A(out_10), .sel(demultiplexer_3_out_0), .D(out_11));
  ROM #(.AddrBits(16), .Bits(8)) rom_2 (.A(out_10), .sel(demultiplexer_3_out_1), .D(out_11));
  ROM #(.AddrBits(16), .Bits(8)) rom_3 (.A(out_10), .sel(demultiplexer_3_out_2), .D(out_11));
  ROM #(.AddrBits(16), .Bits(8)) rom_4 (.A(out_10), .sel(demultiplexer_3_out_3), .D(out_11));
  ROM #(.AddrBits(16), .Bits(8)) rom_5 (.A(out_10), .sel(demultiplexer_3_out_4), .D(out_11));
  ROM #(.AddrBits(16), .Bits(8)) rom_6 (.A(out_10), .sel(demultiplexer_3_out_5), .D(out_11));
  LED led_299 (.in(out_9[0]));
  LED led_300 (.in(out_9[1]));
  LED led_301 (.in(out_9[2]));
  LED led_302 (.in(out_9[3]));
  LED led_303 (.in(out_6[0]));
  LED led_304 (.in(out_6[1]));
  LED led_305 (.in(out_6[2]));
  LED led_306 (.in(out_6[3]));
  LED led_307 (.in(out_12[0]));
  LED led_308 (.in(out_12[1]));
  LED led_309 (.in(out_12[2]));
  LED led_310 (.in(out_12[3]));
  LED led_311 (.in(out_3[0]));
  LED led_312 (.in(out_3[1]));
  LED led_313 (.in(out_3[2]));
  LED led_314 (.in(out_3[3]));
  LED led_315 (.in(decoder_1_out_13));
  LED led_316 (.in(decoder_1_out_12));
  LED led_317 (.in(decoder_1_out_11));
  LED led_318 (.in(decoder_1_out_10));
  Register #(.Bits(8)) register_20 (.D(out_11), .C(CLK_t), .en(OUT), .Q(out_13));
  LED led_319 (.in(out_4[13]));
  LED led_320 (.in(out_4[14]));
  LED led_321 (.in(out_4[15]));
  LED led_322 (.in(out_10[13]));
  LED led_323 (.in(out_10[14]));
  LED led_324 (.in(out_10[15]));
  LED led_325 (.in(decoder_1_out_9));
  LED led_326 (.in(decoder_1_out_8));
  LED led_327 (.in(decoder_1_out_7));
  LED led_328 (.in(decoder_1_out_6));
  PullDown #(.Bits(8)) pulldown_3 (.out(out_11));
  LED led_329 (.in(out_4[9]));
  LED led_330 (.in(out_4[10]));
  LED led_331 (.in(out_4[11]));
  LED led_332 (.in(out_4[12]));
  LED led_333 (.in(out_10[9]));
  LED led_334 (.in(out_10[10]));
  LED led_335 (.in(out_10[11]));
  LED led_336 (.in(out_10[12]));
  LED led_337 (.in(decoder_1_out_5));
  LED led_338 (.in(decoder_1_out_4));
  LED led_339 (.in(decoder_1_out_3));
  LED led_340 (.in(decoder_1_out_2));
  Register #(.Bits(8)) register_21 (.D(out_11), .C(CLK_t), .en(IRI), .Q({register_21_q, out_12}));
  PullDown #(.Bits(8)) pulldown_4 (.out(pulldown_4_out));
  Register #(.Bits(8)) register_22 (.D(out_11), .C(CLK_t), .en(BI), .Q(out_9));
  Register #(.Bits(8)) register_23 (.D(out_11), .C(CLK_t), .en(AI), .Q(out_8));
  assign out_11 = BO ? out_9 : 8'bz;  // Driver driver_3
  assign out_11 = AO ? out_8 : 8'bz;  // Driver driver_4
  PullDown pulldown_5 (.out(driver_6_out[1]));
  LED led_341 (.in(out_4[5]));
  LED led_342 (.in(out_4[6]));
  LED led_343 (.in(out_4[7]));
  LED led_344 (.in(out_4[8]));
  LED led_345 (.in(out_10[5]));
  LED led_346 (.in(out_10[6]));
  LED led_347 (.in(out_10[7]));
  LED led_348 (.in(out_10[8]));
  LED led_349 (.in(out_11[5]));
  LED led_350 (.in(out_11[6]));
  LED led_351 (.in(out_11[7]));
  LED led_352 (.in(out_13[5]));
  LED led_353 (.in(out_13[6]));
  LED led_354 (.in(out_13[7]));
  Decoder #(.Selector_Bits(4)) decoder_1 (
    .sel(CW[3:0]), .out_0(CO1), .out_1(COE1), .out_2(decoder_1_out_2), .out_3(decoder_1_out_3),
    .out_4(decoder_1_out_4), .out_5(decoder_1_out_5), .out_6(decoder_1_out_6), .out_7(decoder_1_out_7),
    .out_8(decoder_1_out_8), .out_9(decoder_1_out_9), .out_10(decoder_1_out_10), .out_11(decoder_1_out_11),
    .out_12(decoder_1_out_12), .out_13(decoder_1_out_13), .out_14(decoder_1_out_14), .out_15(decoder_1_out_15));
  assign pulldown_4_out = SUB ? {8{1'b1}} : 8'bz;  // Driver driver_5
  assign xor_1_out = pulldown_4_out ^ out_9;  // XOr xor_1, 8 bits wide
  LED led_355 (.in(out_4[1]));
  LED led_356 (.in(out_4[2]));
  LED led_357 (.in(out_4[3]));
  LED led_358 (.in(out_4[4]));
  LED led_359 (.in(out_10[1]));
  LED led_360 (.in(out_10[2]));
  LED led_361 (.in(out_10[3]));
  LED led_362 (.in(out_10[4]));
  LED led_363 (.in(out_11[1]));
  LED led_364 (.in(out_11[2]));
  LED led_365 (.in(out_11[3]));
  LED led_366 (.in(out_11[4]));
  LED led_367 (.in(out_13[1]));
  LED led_368 (.in(out_13[2]));
  LED led_369 (.in(out_13[3]));
  LED led_370 (.in(out_13[4]));
  Counter #(.Bits(4)) counter_3 (.en(pullup_2_out), .C(CLK_t), .clr(or_2_out), .out(CW[3:0]), .ovf(counter_3_ovf));
  PullUp pullup_2 (.out(pullup_2_out));
  Comparator #(.Bits(8)) comparator_1 (
    .a(out_8), .b(xor_1_out), .gt(comparator_1_lt[1]), .lt(comparator_1_lt[0]));  // open: eq
  assign driver_6_out = CARO ? comparator_1_lt : 2'bz;  // Driver driver_6
  PullDown pulldown_6 (.out(driver_6_out[0]));
  LED led_371 (.in(out_4[0]));
  LED led_372 (.in(out_10[0]));
  LED led_373 (.in(out_11[0]));
  LED led_374 (.in(out_13[0]));
  or or_2 (or_2_out, NXT, counter_3_ovf);
  Add #(.Bits(8)) add_1 (.a(out_8), .b(xor_1_out), .c_i(SUB), .s(out_5), .c_o(add_1_c_o));
  assign out_11 = ADO ? out_5 : 8'bz;  // Driver driver_7
  assign driver_8_out[1] = CARO ? add_1_c_o : 1'bz;  // Driver driver_8
  PullDown pulldown_7 (.out(driver_8_out[1]));
  PullDown #(.Bits(4)) pulldown_8 (.out(CW[11:8]));
  BarrelShifter #(.Bits(8)) barrelshifter_1 (.in(out_8), .shift(xor_1_out[3:0]), .out(out_2));
  assign out_11 = SAO ? out_2 : 8'bz;  // Driver driver_9
  PullDown pulldown_9 (.out(driver_8_out[0]));
  ROM #(.AddrBits(16), .Bits(24)) rom_7 (
    .A({out_12, CW[11:8], out_3, CW[3:0]}), .sel(pullup_3_out),
    .D({MAR, MI, NXT, OUT, CLR2, HLT, IRI2, FI, CARO, rom_7_d[14], RAO2, MRI2, CI, COE2, CO2, LBI, HBI, SUB, SAO, ADO, BO, AO, BI, AI}));
  PullUp pullup_3 (.out(pullup_3_out));
  Register #(.Bits(4)) register_24 (.D({driver_6_out, driver_8_out}), .C(CLK_t), .en(FI), .Q(out_3));
  PullDown pulldown_10 (.out(rom_7_d[14]));
  nor nor_1 (nor_1_out, out_8[0], out_8[1], out_8[2], out_8[3], out_8[4], out_8[5], out_8[6], out_8[7]);
  assign driver_8_out[0] = CARO ? nor_1_out : 1'bz;  // Driver driver_10
  or or_3 (MRI, CO1, MRI2);
  or or_4 (CO, CO1, CO2);
  or or_5 (COE, COE1, COE2);
  or or_6 (RAO, COE1, RAO2);
  or or_7 (IRI, COE1, IRI2);
  or or_8 (CLR, CLR1, CLR2);

  // Other names for the same wires on the sheet: CW (some bits) = {out_12, out_3}; IRP[3:0] = out_12;
  //   ADP[7:0] = out_5; AP[7:0] = out_8; BP[7:0] = out_9; BUS[7:0] = out_11; FO[3:0] = out_3; HBP[7:0] = out_7;
  //   LBP[7:0] = out_6; MRI1 = CO1; MRP[15:0] = out_10; OUP[7:0] = out_13; PCP[15:0] = out_4; IRI1 = COE1;
  //   RAO1 = COE1; SAP[7:0] = out_2

  // Notes on the sheet:
  //   clk: Hz: 2500
  //   Graphics Logic
  //   16x16 LED Matrix
  //   Clock
  //   Probes
  //   CPU
  //   rom_1 loads baddapplehex0.hex
  //   contents of rom_2 (hex, n*v repeats v):
  //   5,ff,ff,5,ff,ff,5,ff,ff,5,ff,ff,5,ff,ff,5,ff,ff,5,ff,ff,5,ff,ff
  //   ,5,ff,ff,5,ff,ff,5,ff,ff,5,ff,ff,5,ff,ff,5,ff,ff,5,ff,ff,5,ff,ff
  //   ,5,ff,ff,5,ff,ff,5,ff,ff,5,ff,ff,5,ff,ff,5,ff,ff,5,ff,ff,5,ff,ff
  //   ,5,ff,ff,5,ff,ff,5,ff,ff,5,ff,ff,5,ff,ff,5,ff,ff,5,ff,ff,5,ff,ff
  //   ,5,ff,ff,5,ff,ff,5,ff,ff,5,ff,ff,5,ff,ff,5,ff,ff,5,ff,ff,5,ff,ff
  //   ,5,ff,ff,5,ff,ff,5,ff,ff,5,ff,ff,5,ff,ff,5,ff,ff,5,ff,ff,5,ff,ff
  //   ,5,ff,ff,5,ff,ff,5,ff,ff,5,ff,ff,5,ff,ff,5,ff,ff,5,ff,ff,5,ff,ff
  //   ,5,ff,ff,5,ff,ff,5,ff,ff,5,ff,ff,5,ff,ff,5,ff,ff,5,ff,ff,5,ff,ff
  //   ,5,ff,ff,5,ff,ff,5,ff,ff,5,ff,ff,5,ff,ff,5,ff,ff,5,ff,ff,5,ff,ff
  //   ,5,ff,ff,5,ff,ff,5,ff,ff,5,ff,ff,5,ff,ff,5,ff,ff,5,ff,ff,5,ff,ff
  //   ,5,ff,ff,5,ff,ff,5,ff,ff,5,ff,ff,5,ff,ff,5,ff,ff,5,ff,ff,5,ff,ff
  //   ,5,ff,ff,5,ff,ff,5,ff,ff,5,ff,ff,5,ff,ff,5,ff,ff,5,ff,ff,5,ff,ff
  //   ,5,ff,ff,5,ff,ff,5,ff,ff,5,ff,ff,5,ff,ff,5,ff,ff,5,ff,ff,5,ff,ff
  //   ,5,ff,ff,5,ff,ff,5,ff,ff,5,ff,ff,5,ff,ff,5,ff,ff,5,ff,ff,5,ff,ff
  //   ,5,ff,ff,5,ff,ff,5,ff,ff,5,ff,ff,5,ff,ff,5,ff,ff,5,ff,ff,5,ff,ff
  //   ,5,ff,ff,5,ff,ff,5,ff,ff,5,ff,ff,5,ff,ff,5,ff,ff,5,ff,ff,5,ff,ff
  //   ,5,ff,ff,5,ff,ff,5,ff,ff,5,ff,ff,5,ff,ff,5,ff,ff,5,ff,ff,5,ff,ff
  //   ,5,ff,ff,5,ff,ff,5,ff,ff,5,ff,ff,5,ff,ff,5,ff,ff,5,ff,ff,5,ff,ff
  //   ,5,ff,ff,5,ff,ff,5,ff,ff,5,ff,ff,5,ff,ff,5,ff,ff,5,ff,ff,5,ff,ff
  //   ,5,ff,ff,5,ff,ff,5,ff,ff,5,ff,ff,5,ff,ff,5,ff,ff,5,ff,ff,5,ff,ff
  //   ,5,ff,ff,5,ff,ff,5,ff,ff,5,ff,ff,5,ff,ff,5,ff,ff,5,ff,ff,5,ff,ff
  //   ,5,ff,ff,5,ff,ff,5,ff,ff,5,ff,ff,5,ff,ff,5,ff,ff,5,ff,ff,5,ff,ff
  //   ,5,ff,ff,5,ff,ff,5,ff,ff,5,ff,ff,5,ff,ff,5,ff,ff,5,ff,ff,5,ff,ff
  //   ,5,ff,ff,5,ff,ff,5,ff,ff,5,ff,ff,5,ff,ff,5,ff,ff,5,ff,ff,5,ff,ff
  //   ,5,ff,ff,5,ff,ff,5,ff,ff,5,ff,ff,5,ff,ff,5,ff,ff,5,ff,ff,5,ff,ff
  //   ,5,ff,ff,5,ff,ff,5,ff,ff,5,ff,ff,5,ff,ff,5,ff,ff,5,ff,ff,5,ff,ff
  //   ,5,ff,ff,5,ff,ff,5,ff,ff,5,ff,ff,5,ff,ff,5,ff,ff,5,ff,ff,5,ff,ff
  //   ,5,ff,ff,5,ff,ff,5,ff,ff,5,ff,ff,5,ff,ff,5,ff,ff,5,ff,ff,5,ff,ff
  //   ,5,ff,ff,5,ff,ff,5,ff,ff,5,ff,ff,5,ff,ff,5,ff,ff,5,ff,ff,5,ff,ff
  //   ,5,ff,ff,5,ff,ff,5,ff,ff,5,ff,ff,5,ff,ff,5,ff,ff,5,ff,ff,5,ff,ff
  //   ,5,ff,ff,5,ff,ff,5,ff,ff,5,ff,ff,5,ff,ff,5,ff,ff,5,ff,ff,5,ff,ff
  //   ,5,ff,ff,5,ff,ff,5,ff,ff,5,ff,ff,5,ff,ff,5,ff,ff,5,ff,ff,5,ff,ff
  //   ,5,ff,ff,5,ff,ff,5,ff,ff,5,ff,ff,5,ff,ff,5,ff,ff,5,ff,ff,5,ff,ff
  //   ,5,ff,ff,5,ff,ff,5,ff,ff,5,ff,ff,5,ff,ff,5,ff,ff,5,ff,ff,5,ff,ff
  //   ,5,ff,ff,5,ff,ff,5,ff,ff,5,ff,ff,5,ff,ff,5,ff,ff,5,ff,ff,5,ff,ff
  //   ,5,ff,ff,5,ff,ff,5,ff,ff,5,ff,ff,5,ff,ff,5,ff,ff,5,ff,ff,5,ff,ff
  //   ,5,ff,ff,5,ff,ff,5,ff,ff,5,ff,ff,5,ff,ff,5,ff,ff,5,ff,ff,5,ff,ff
  //   ,5,ff,ff,5,ff,ff,5,ff,ff,5,ff,ff,5,ff,ff,5,ff,ff,5,ff,ff,5,ff,ff
  //   ,5,ff,ff,5,ff,ff,5,ff,ff,5,ff,ff,5,ff,ff,5,ff,ff,5,ff,ff,5,ff,ff
  //   ,5,ff,ff,5,ff,ff,5,ff,ff,5,ff,ff,5,ff,ff,5,ff,ff,5,ff,ff,5,ff,ff
  //   ,5,ff,ff,5,ff,ff,5,ff,ff,5,ff,ff,5,ff,ff,5,ff,ff,5,ff,ff,5,ff,ff
  //   ,5,ff,ff,5,ff,ff,5,ff,ff,5,ff,ff,5,ff,ff,5,ff,ff,5,ff,ff,5,ff,ff
  //   ,5,ff,ff,5,ff,ff,5,ff,ff,5,ff,ff,5,ff,ff,5,ff,ff,5,ff,ff,5,ff,ff
  //   ,5,ff,ff,5,ff,ff,5,ff,ff,5,ff,ff,5,ff,ff,5,ff,ff,5,ff,ff,5,ff,ff
  //   ,5,ff,ff,5,ff,ff,5,ff,ff,5,ff,ff,5,ff,ff,5,ff,ff,5,ff,ff,5,ff,ff
  //   ,5,ff,ff,5,ff,ff,5,ff,ff,5,ff,ff,5,ff,ff,5,ff,ff,5,ff,ff,5,ff,ff
  //   ,5,ff,ff,5,ff,ff,5,ff,ff,5,ff,ff,5,ff,ff,5,ff,ff,5,ff,ff,5,ff,ff
  //   ,5,ff,ff,5,ff,ff,5,ff,ff,5,ff,ff,5,ff,ff,5,ff,ff,5,ff,ff,5,ff,ff
  //   ,5,ff,ff,5,ff,ff,5,ff,ff,5,ff,ff,5,ff,ff,5,ff,ff,5,ff,ff,5,ff,ff
  //   ,5,ff,ff,5,ff,ff,5,ff,ff,5,ff,ff,5,ff,ff,5,ff,ff,5,ff,ff,5,ff,ff
  //   ,5,ff,ff,5,ff,ff,5,ff,ff,5,ff,ff,5,ff,ff,5,ff,ff,5,ff,ff,5,ff,ff
  //   ,5,ff,ff,5,ff,ff,5,ff,ff,5,ff,ff,5,ff,ff,5,ff,ff,5,ff,ff,5,ff,ff
  //   ,5,ff,ff,5,ff,ff,5,ff,ff,5,ff,ff,5,ff,ff,5,ff,ff,5,ff,ff,5,ff,ff
  //   ,5,ff,ff,5,ff,ff,5,ff,ff,5,ff,ff,5,ff,ff,5,ff,ff,5,ff,ff,5,ff,ff
  //   ,5,ff,ff,5,ff,ff,5,ff,ff,5,ff,ff,5,ff,ff,5,ff,ff,5,ff,ff,5,ff,ff
  //   ,5,ff,ff,5,ff,ff,5,ff,ff,5,ff,ff,5,ff,ff,5,ff,ff,5,ff,ff,5,ff,ff
  //   ,5,ff,ff,5,ff,ff,5,ff,ff,5,ff,ff,5,ff,ff,5,ff,ff,5,ff,ff,5,ff,ff
  //   ,5,ff,ff,5,ff,ff,5,ff,ff,5,ff,ff,5,ff,ff,5,ff,ff,5,ff,ff,5,ff,ff
  //   ,5,ff,ff,5,ff,ff,5,ff,ff,5,ff,ff,5,ff,ff,5,ff,ff,5,ff,ff,5,ff,ff
  //   ,5,ff,ff,5,ff,ff,5,ff,ff,5,ff,ff,5,ff,ff,5,ff,ff,5,ff,ff,5,ff,ff
  //   ,5,ff,ff,5,ff,ff,5,ff,ff,5,ff,ff,5,ff,ff,5,ff,ff,5,ff,ff,5,ff,ff
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  //   contents of rom_3 (hex, n*v repeats v):
  //   5,ff,ff,5,ff,ff,5,ff,ff,5,ff,ff,5,ff,ff,5,ff,ff,5,ff,ff,5,ff,ff
  //   ,5,ff,ff,5,ff,ff,5,ff,ff,5,ff,ff,5,ff,ff,5,ff,ff,5,ff,ff,5,ff,ff
  //   ,5,ff,ff,5,ff,ff,5,ff,ff,5,ff,ff,5,ff,ff,5,ff,ff,5,ff,ff,5,ff,ff
  //   ,5,ff,ff,5,ff,ff,5,ff,ff,5,ff,ff,5,ff,ff,5,ff,ff,5,ff,ff,5,ff,ff
  //   ,5,ff,ff,5,ff,ff,5,ff,ff,5,ff,ff,5,ff,ff,5,ff,ff,5,ff,ff,5,ff,ff
  //   ,5,ff,ff,5,ff,ff,5,ff,ff,5,ff,ff,5,ff,ff,5,ff,ff,5,ff,ff,5,ff,ff
  //   ,5,ff,ff,5,ff,ff,5,ff,ff,5,ff,ff,5,ff,ff,5,ff,ff,5,ff,ff,5,ff,ff
  //   ,5,ff,ff,5,ff,ff,5,ff,ff,5,ff,ff,5,ff,ff,5,ff,ff,5,ff,ff,5,ff,ff
  //   ,5,ff,ff,5,ff,ff,5,ff,ff,5,ff,ff,5,ff,ff,5,ff,ff,5,ff,ff,5,ff,ff
  //   ,5,ff,ff,5,ff,ff,5,ff,ff,5,ff,ff,5,ff,ff,5,ff,ff,5,ff,ff,5,ff,ff
  //   ,5,ff,ff,5,ff,ff,5,ff,ff,5,ff,ff,5,ff,ff,5,ff,ff,5,ff,ff,5,ff,ff
  //   ,5,ff,ff,5,ff,ff,5,ff,ff,5,ff,ff,5,ff,ff,5,ff,ff,5,ff,ff,5,ff,ff
  //   ,5,ff,ff,5,ff,ff,5,ff,ff,5,ff,ff,5,ff,ff,5,ff,ff,5,ff,ff,5,ff,ff
  //   ,5,ff,ff,5,ff,ff,5,ff,ff,5,ff,ff,5,ff,ff,5,ff,ff,5,ff,ff,5,ff,ff
  //   ,5,ff,ff,5,ff,ff,5,ff,ff,5,ff,ff,5,ff,ff,5,ff,ff,5,ff,ff,5,ff,ff
  //   ,5,ff,ff,5,ff,ff,5,ff,ff,5,ff,ff,5,ff,ff,5,ff,ff,5,ff,ff,5,ff,ff
  //   ,5,ff,ff,5,ff,ff,5,ff,ff,5,ff,ff,5,ff,ff,5,ff,ff,5,ff,ff,5,ff,ff
  //   ,5,ff,ff,5,ff,ff,5,ff,ff,5,ff,ff,5,ff,ff,5,ff,ff,5,ff,ff,5,ff,ff
  //   ,5,ff,ff,5,ff,ff,5,ff,ff,5,ff,ff,5,ff,ff,5,ff,ff,5,ff,ff,5,ff,ff
  //   ,5,ff,ff,5,ff,ff,5,ff,ff,5,ff,ff,5,ff,ff,5,ff,ff,5,ff,ff,5,ff,ff
  //   ,5,ff,ff,5,ff,ff,5,ff,ff,5,ff,ff,5,ff,ff,5,ff,ff,5,ff,ff,5,ff,ff
  //   ,5,ff,ff,5,ff,ff,5,ff,ff,5,ff,ff,5,ff,ff,5,ff,ff,5,ff,ff,5,ff,ff
  //   ,5,ff,ff,5,ff,ff,5,ff,ff,5,ff,ff,5,ff,ff,5,ff,ff,5,ff,ff,5,ff,ff
  //   ,5,ff,ff,5,ff,ff,5,ff,ff,5,ff,ff,5,ff,ff,5,ff,ff,5,ff,ff,5,ff,ff
  //   ,5,ff,ff,5,ff,ff,5,ff,ff,5,ff,ff,5,ff,ff,5,ff,ff,5,ff,ff,5,ff,ff
  //   ,5,ff,ff,5,ff,ff,5,ff,ff,5,ff,ff,5,ff,ff,5,ff,ff,5,ff,ff,5,ff,ff
  //   ,5,ff,ff,5,ff,ff,5,ff,ff,5,ff,ff,5,ff,ff,5,ff,ff,5,ff,ff,5,ff,ff
  //   ,5,ff,ff,5,ff,ff,5,ff,ff,5,ff,ff,5,ff,ff,5,ff,ff,5,ff,ff,5,ff,ff
  //   ,5,ff,ff,5,ff,ff,5,ff,ff,5,ff,ff,5,ff,ff,5,ff,ff,5,ff,ff,5,ff,ff
  //   ,5,ff,ff,5,ff,ff,5,ff,ff,5,ff,ff,5,ff,ff,5,ff,ff,5,ff,ff,5,ff,ff
  //   ,5,ff,ff,5,ff,ff,5,ff,ff,5,ff,ff,5,ff,ff,5,ff,ff,5,ff,ff,5,ff,ff
  //   ,5,ff,ff,5,ff,ff,5,ff,ff,5,ff,ff,5,ff,ff,5,ff,ff,5,ff,ff,5,ff,ff
  //   ,5,ff,ff,5,ff,ff,5,ff,ff,5,ff,ff,5,ff,ff,5,ff,ff,5,ff,ff,5,ff,ff
  //   ,5,ff,ff,5,ff,ff,5,ff,ff,5,ff,ff,5,ff,ff,5,ff,ff,5,ff,ff,5,ff,ff
  //   ,5,ff,ff,5,ff,ff,5,ff,ff,5,ff,ff,5,ff,ff,5,ff,ff,5,ff,ff,5,ff,ff
  //   ,5,ff,ff,5,ff,ff,5,ff,ff,5,ff,ff,5,ff,ff,5,ff,ff,5,ff,ff,5,ff,ff
  //   ,5,ff,ff,5,ff,ff,5,ff,ff,5,ff,ff,5,ff,ff,5,ff,ff,5,ff,ff,5,ff,ff
  //   ,5,ff,ff,5,ff,ff,5,ff,ff,5,ff,ff,5,ff,ff,5,ff,ff,5,ff,ff,5,ff,ff
  //   ,5,ff,ff,5,ff,ff,5,ff,ff,5,ff,ff,5,ff,ff,5,ff,ff,5,ff,ff,5,ff,ff
  //   ,5,ff,ff,5,ff,ff,5,ff,ff,5,ff,ff,5,ff,ff,5,ff,ff,5,ff,ff,5,ff,ff
  //   ,5,ff,ff,5,ff,ff,5,ff,ff,5,ff,ff,5,ff,ff,5,ff,ff,5,ff,ff,5,ff,ff
  //   ,5,ff,ff,5,ff,ff,5,ff,ff,5,ff,ff,5,ff,ff,5,ff,ff,5,ff,ff,5,ff,ff
  //   ,5,ff,ff,5,ff,ff,5,ff,ff,5,ff,ff,5,ff,ff,5,ff,ff,5,ff,ff,5,ff,ff
  //   ,5,ff,ff,5,ff,ff,5,ff,ff,5,ff,ff,5,ff,ff,5,ff,ff,5,ff,ff,5,ff,ff
  //   ,5,ff,ff,5,ff,ff,5,ff,ff,5,ff,ff,5,ff,ff,5,ff,ff,5,ff,ff,5,ff,ff
  //   ,5,ff,ff,5,ff,ff,5,ff,ff,5,ff,ff,5,ff,ff,5,ff,ff,5,ff,ff,5,ff,ff
  //   ,5,ff,ff,5,ff,ff,5,ff,ff,5,ff,ff,5,ff,ff,5,ff,ff,5,ff,ff,5,ff,ff
  //   ,5,ff,ff,5,ff,ff,5,ff,ff,5,ff,ff,5,ff,ff,5,ff,ff,5,ff,ff,5,ff,ff
  //   ,5,ff,ff,5,ff,ff,5,ff,ff,5,ff,ff,5,ff,ff,5,ff,ff,5,ff,ff,5,ff,ff
  //   ,5,ff,ff,5,ff,ff,5,ff,ff,5,ff,ff,5,ff,ff,5,ff,ff,5,ff,ff,5,ff,ff
  //   ,5,ff,ff,5,ff,ff,5,ff,ff,5,ff,ff,5,ff,ff,5,ff,ff,5,ff,ff,5,ff,ff
  //   ,5,ff,ff,5,ff,ff,5,ff,ff,5,ff,ff,5,ff,ff,5,ff,ff,5,ff,ff,5,ff,ff
  //   ,5,ff,ff,5,ff,ff,5,ff,ff,5,ff,ff,5,ff,ff,5,ff,ff,5,ff,ff,5,ff,ff
  //   ,5,ff,ff,5,ff,ff,5,ff,ff,5,ff,ff,5,ff,ff,5,ff,ff,5,ff,ff,5,ff,ff
  //   ,5,ff,ff,5,ff,ff,5,ff,ff,5,ff,ff,5,ff,ff,5,ff,ff,5,ff,ff,5,ff,ff
  //   ,5,ff,ff,5,ff,ff,5,ff,ff,5,ff,ff,5,ff,ff,5,ff,ff,5,ff,ff,5,ff,ff
  //   ,5,ff,ff,5,ff,ff,5,ff,ff,5,ff,ff,5,ff,ff,5,ff,ff,5,ff,ff,5,ff,ff
  //   ,5,ff,ff,5,ff,ff,5,ff,ff,5,ff,ff,5,ff,ff,5,ff,ff,5,ff,ff,5,ff,ff
  //   ,5,ff,ff,5,ff,ff,5,ff,ff,5,ff,ff,5,ff,ff,5,ff,ff,5,ff,ff,5,ff,ff
  //   ,5,ff,ff,5,ff,ff,5,ff,ff,5,ff,ff,5,ff,ff,5,ff,ff,5,ff,ff,5,ff,ff
  //   ,5,ff,ff,5,ff,ff,5,ff,ff,5,ff,ff,5,ff,ff,5,ff,ff,5,ff,ff,5,ff,ff
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  //   contents of rom_4 (hex, n*v repeats v):
  //   5,ff,ff,5,ff,ff,5,ff,ff,5,ff,ff,5,ff,ff,5,ff,ff,5,ff,ff,5,ff,ff
  //   ,5,ff,ff,5,ff,ff,5,ff,ff,5,ff,ff,5,ff,ff,5,ff,ff,5,ff,ff,5,ff,ff
  //   ,5,ff,ff,5,ff,ff,5,ff,ff,5,ff,ff,5,ff,ff,5,ff,ff,5,ff,ff,5,ff,ff
  //   ,5,ff,ff,5,ff,ff,5,ff,ff,5,ff,ff,5,ff,ff,5,ff,ff,5,ff,ff,5,ff,ff
  //   ,5,ff,ff,5,ff,ff,5,ff,ff,5,ff,ff,5,ff,ff,5,ff,ff,5,ff,ff,5,ff,ff
  //   ,5,ff,ff,5,ff,ff,5,ff,ff,5,ff,ff,5,ff,ff,5,ff,ff,5,ff,ff,5,ff,ff
  //   ,5,ff,ff,5,ff,ff,5,ff,ff,5,ff,ff,5,ff,ff,5,ff,ff,5,ff,ff,5,ff,ff
  //   ,5,ff,ff,5,ff,ff,5,ff,ff,5,ff,ff,5,ff,ff,5,ff,ff,5,ff,ff,5,ff,ff
  //   ,5,ff,ff,5,ff,ff,5,ff,ff,5,ff,ff,5,ff,ff,5,ff,ff,5,ff,ff,5,ff,ff
  //   ,5,ff,ff,5,ff,ff,5,ff,ff,5,ff,ff,5,ff,ff,5,ff,ff,5,ff,ff,5,ff,ff
  //   ,5,ff,ff,5,ff,ff,5,ff,ff,5,ff,ff,5,ff,ff,5,ff,ff,5,ff,ff,5,ff,ff
  //   ,5,ff,ff,5,ff,ff,5,ff,ff,5,ff,ff,5,ff,ff,5,ff,ff,5,ff,ff,5,ff,ff
  //   ,5,ff,ff,5,ff,ff,5,ff,ff,5,ff,ff,5,ff,ff,5,ff,ff,5,ff,ff,5,ff,ff
  //   ,5,ff,ff,5,ff,ff,5,ff,ff,5,ff,ff,5,ff,ff,5,ff,ff,5,ff,ff,5,ff,ff
  //   ,5,ff,ff,5,ff,ff,5,ff,ff,5,ff,ff,5,ff,ff,5,ff,ff,5,ff,ff,5,ff,ff
  //   ,5,ff,ff,5,ff,ff,5,ff,ff,5,ff,ff,5,ff,ff,5,ff,ff,5,ff,ff,5,ff,ff
  //   ,5,ff,ff,5,ff,ff,5,ff,ff,5,ff,ff,5,ff,ff,5,ff,ff,5,ff,ff,5,ff,ff
  //   ,5,ff,ff,5,ff,ff,5,ff,ff,5,ff,ff,5,ff,ff,5,ff,ff,5,ff,ff,5,ff,ff
  //   ,5,ff,ff,5,ff,ff,5,ff,ff,5,ff,ff,5,ff,ff,5,ff,ff,5,ff,ff,5,ff,ff
  //   ,5,ff,ff,5,ff,ff,5,ff,ff,5,ff,ff,5,ff,ff,5,ff,ff,5,ff,ff,5,ff,ff
  //   ,5,ff,ff,5,ff,ff,5,ff,ff,5,ff,ff,5,ff,ff,5,ff,ff,5,ff,ff,5,ff,ff
  //   ,5,ff,ff,5,ff,ff,5,ff,ff,5,ff,ff,5,ff,ff,5,ff,ff,5,ff,ff,5,ff,ff
  //   ,5,ff,ff,5,ff,ff,5,ff,ff,5,ff,ff,5,ff,ff,5,ff,ff,5,ff,ff,5,ff,ff
  //   ,5,ff,ff,5,ff,ff,5,ff,ff,5,ff,ff,5,ff,ff,5,ff,ff,5,ff,ff,5,ff,ff
  //   ,5,ff,ff,5,ff,ff,5,ff,ff,5,ff,ff,5,ff,ff,5,ff,ff,5,ff,ff,5,ff,ff
  //   ,5,ff,ff,5,ff,ff,5,ff,ff,5,ff,ff,5,ff,ff,5,ff,ff,5,ff,ff,5,ff,ff
  //   ,5,ff,ff,5,ff,ff,5,ff,ff,5,ff,ff,5,ff,ff,5,ff,ff,5,ff,ff,5,ff,ff
  //   ,5,ff,ff,5,ff,ff,5,ff,ff,5,ff,ff,5,ff,ff,5,ff,ff,5,ff,ff,5,ff,ff
  //   ,5,ff,ff,5,ff,ff,5,ff,ff,5,ff,ff,5,ff,ff,5,ff,ff,5,ff,ff,5,ff,ff
  //   ,5,ff,ff,5,ff,ff,5,ff,ff,5,ff,ff,5,ff,ff,5,ff,ff,5,ff,ff,5,ff,ff
  //   ,5,ff,ff,5,ff,ff,5,ff,ff,5,ff,ff,5,ff,ff,5,ff,ff,5,ff,ff,5,ff,ff
  //   ,5,ff,ff,5,ff,ff,5,ff,ff,5,ff,ff,5,ff,ff,5,ff,ff,5,ff,ff,5,ff,ff
  //   ,5,ff,ff,5,ff,ff,5,ff,ff,5,ff,ff,5,ff,ff,5,ff,ff,5,ff,ff,5,ff,ff
  //   ,5,ff,ff,5,ff,ff,5,ff,ff,5,ff,ff,5,ff,ff,5,ff,ff,5,ff,ff,5,ff,ff
  //   ,5,ff,ff,5,ff,ff,5,ff,ff,5,ff,ff,5,ff,ff,5,ff,ff,5,ff,ff,5,ff,ff
  //   ,5,ff,ff,5,ff,ff,5,ff,ff,5,ff,ff,5,ff,ff,5,ff,ff,5,ff,ff,5,ff,ff
  //   ,5,ff,ff,5,ff,ff,5,ff,ff,5,ff,ff,5,ff,ff,5,ff,ff,5,ff,ff,5,ff,ff
  //   ,5,ff,ff,5,ff,ff,5,ff,ff,5,ff,ff,5,ff,ff,5,ff,ff,5,ff,ff,5,ff,ff
  //   ,5,ff,ff,5,ff,ff,5,ff,ff,5,ff,ff,5,ff,ff,5,ff,ff,5,ff,ff,5,ff,ff
  //   ,5,ff,ff,5,ff,ff,5,ff,ff,5,ff,ff,5,ff,ff,5,ff,ff,5,ff,ff,5,ff,ff
  //   ,5,ff,ff,5,ff,ff,5,ff,ff,5,ff,ff,5,ff,ff,5,ff,ff,5,ff,ff,5,ff,ff
  //   ,5,ff,ff,5,ff,ff,5,ff,ff,5,ff,ff,5,ff,ff,5,ff,ff,5,ff,ff,5,ff,ff
  //   ,5,ff,ff,5,ff,ff,5,ff,ff,5,ff,ff,5,ff,ff,5,ff,ff,5,ff,ff,5,ff,ff
  //   ,5,ff,ff,5,ff,ff,5,ff,ff,5,ff,ff,5,ff,ff,5,ff,ff,5,ff,ff,5,ff,ff
  //   ,5,ff,ff,5,ff,ff,5,ff,ff,5,ff,ff,5,ff,ff,5,ff,ff,5,ff,ff,5,ff,ff
  //   ,5,ff,ff,5,ff,ff,5,ff,ff,5,ff,ff,5,ff,ff,5,ff,ff,5,ff,ff,5,ff,ff
  //   ,5,ff,ff,5,ff,ff,5,ff,ff,5,ff,ff,5,ff,ff,5,ff,ff,5,ff,ff,5,ff,ff
  //   ,5,ff,ff,5,ff,ff,5,ff,ff,5,ff,ff,5,ff,ff,5,ff,ff,5,ff,ff,5,ff,ff
  //   ,5,ff,ff,5,ff,ff,5,ff,ff,5,ff,ff,5,ff,ff,5,ff,ff,5,ff,ff,5,ff,ff
  //   ,5,ff,ff,5,ff,ff,5,ff,ff,5,ff,ff,5,ff,ff,5,ff,ff,5,ff,ff,5,ff,ff
  //   ,5,ff,ff,5,ff,ff,5,ff,ff,5,ff,ff,5,ff,ff,5,ff,ff,5,ff,ff,5,ff,ff
  //   ,5,ff,ff,5,ff,ff,5,ff,ff,5,ff,ff,5,ff,ff,5,ff,ff,5,ff,ff,5,ff,ff
  //   ,5,ff,ff,5,ff,ff,5,ff,ff,5,ff,ff,5,ff,ff,5,ff,ff,5,ff,ff,5,ff,ff
  //   ,5,ff,ff,5,ff,ff,5,ff,ff,5,ff,ff,5,ff,ff,5,ff,ff,5,ff,ff,5,ff,ff
  //   ,5,ff,ff,5,ff,ff,5,ff,ff,5,ff,ff,5,ff,ff,5,ff,ff,5,ff,ff,5,ff,ff
  //   ,5,ff,ff,5,ff,ff,5,ff,ff,5,ff,ff,5,ff,ff,5,ff,ff,5,ff,ff,5,ff,ff
  //   ,5,ff,ff,5,ff,ff,5,ff,ff,5,ff,ff,5,ff,ff,5,ff,ff,5,ff,ff,5,ff,ff
  //   ,5,ff,ff,5,ff,ff,5,ff,ff,5,ff,ff,5,ff,ff,5,ff,ff,5,ff,ff,5,ff,ff
  //   ,5,ff,ff,5,ff,ff,5,ff,ff,5,ff,ff,5,ff,ff,5,ff,ff,5,ff,ff,5,ff,ff
  //   ,5,ff,ff,5,ff,ff,5,ff,ff,5,ff,ff,5,ff,ff,5,ff,ff,5,ff,ff,5,ff,ff
  //   ,5,ff,ff,5,ff,ff,5,ff,ff,5,ff,ff,5,ff,ff,5,ff,ff,5,ff,ff,5,ff,ff
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  //   contents of rom_5 (hex, n*v repeats v):
  //   5,ff,ff,5,ff,ff,5,ff,ff,5,ff,ff,5,ff,ff,5,ff,ff,5,ff,ff,5,ff,ff
  //   ,5,ff,ff,5,ff,ff,5,ff,ff,5,ff,ff,5,ff,ff,5,ff,ff,5,ff,ff,5,ff,ff
  //   ,5,ff,ff,5,ff,ff,5,ff,ff,5,ff,ff,5,ff,ff,5,ff,ff,5,ff,ff,5,ff,ff
  //   ,5,ff,ff,5,ff,ff,5,ff,ff,5,ff,ff,5,ff,ff,5,ff,ff,5,ff,ff,5,ff,ff
  //   ,5,ff,ff,5,ff,ff,5,ff,ff,5,ff,ff,5,ff,ff,5,ff,ff,5,ff,ff,5,ff,ff
  //   ,5,ff,ff,5,ff,ff,5,ff,ff,5,ff,ff,5,ff,ff,5,ff,ff,5,ff,ff,5,ff,ff
  //   ,5,ff,ff,5,ff,ff,5,ff,ff,5,ff,ff,5,ff,ff,5,ff,ff,5,ff,ff,5,ff,ff
  //   ,5,ff,ff,5,ff,ff,5,ff,ff,5,ff,ff,5,ff,ff,5,ff,ff,5,ff,ff,5,ff,ff
  //   ,5,ff,ff,5,ff,ff,5,ff,ff,5,ff,ff,5,ff,ff,5,ff,ff,5,ff,ff,5,ff,ff
  //   ,5,ff,ff,5,ff,ff,5,ff,ff,5,ff,ff,5,ff,ff,5,ff,ff,5,ff,ff,5,ff,ff
  //   ,5,ff,ff,5,ff,ff,5,ff,ff,5,ff,ff,5,ff,ff,5,ff,ff,5,ff,ff,5,ff,ff
  //   ,5,ff,ff,5,ff,ff,5,ff,ff,5,ff,ff,5,ff,ff,5,ff,ff,5,ff,ff,5,ff,ff
  //   ,5,ff,ff,5,ff,ff,5,ff,ff,5,ff,ff,5,ff,ff,5,ff,ff,5,ff,ff,5,ff,ff
  //   ,5,ff,ff,5,ff,ff,5,ff,ff,5,ff,ff,5,ff,ff,5,ff,ff,5,ff,ff,5,ff,ff
  //   ,5,ff,ff,5,ff,ff,5,ff,ff,5,ff,ff,5,ff,ff,5,ff,ff,5,ff,ff,5,ff,ff
  //   ,5,ff,ff,5,ff,ff,5,ff,ff,5,ff,ff,5,ff,ff,5,ff,ff,5,ff,ff,5,ff,ff
  //   ,5,ff,ff,5,ff,ff,5,ff,ff,5,ff,ff,5,ff,ff,5,ff,ff,5,ff,ff,5,ff,ff
  //   ,5,ff,ff,5,ff,ff,5,ff,ff,5,ff,ff,5,ff,ff,5,ff,ff,5,ff,ff,5,ff,ff
  //   ,5,ff,ff,5,ff,ff,5,ff,ff,5,ff,ff,5,ff,ff,5,ff,ff,5,ff,ff,5,ff,ff
  //   ,5,ff,ff,5,ff,ff,5,ff,ff,5,ff,ff,5,ff,ff,5,ff,ff,5,ff,ff,5,ff,ff
  //   ,5,ff,ff,5,ff,ff,5,ff,ff,5,ff,ff,5,ff,ff,5,ff,ff,5,ff,ff,5,ff,ff
  //   ,5,ff,ff,5,ff,ff,5,ff,ff,5,ff,ff,5,ff,ff,5,ff,ff,5,ff,ff,5,ff,ff
  //   ,5,ff,ff,5,ff,ff,5,ff,ff,5,ff,ff,5,ff,ff,5,ff,ff,5,ff,ff,5,ff,ff
  //   ,5,ff,ff,5,ff,ff,5,ff,ff,5,ff,ff,5,ff,ff,5,ff,ff,5,ff,ff,5,ff,ff
  //   ,5,ff,ff,5,ff,ff,5,ff,ff,5,ff,ff,5,ff,ff,5,ff,ff,5,ff,ff,5,ff,ff
  //   ,5,ff,ff,5,ff,ff,5,ff,ff,5,ff,ff,5,ff,ff,5,ff,ff,5,ff,ff,5,ff,ff
  //   ,5,ff,ff,5,ff,ff,5,ff,ff,5,ff,ff,5,ff,ff,5,ff,ff,5,ff,ff,5,ff,ff
  //   ,5,ff,ff,5,ff,ff,5,ff,ff,5,ff,ff,5,ff,ff,5,ff,ff,5,ff,ff,5,ff,ff
  //   ,5,ff,ff,5,ff,ff,5,ff,ff,5,ff,ff,5,ff,ff,5,ff,ff,5,ff,ff,5,ff,ff
  //   ,5,ff,ff,5,ff,ff,5,ff,ff,5,ff,ff,5,ff,ff,5,ff,ff,5,ff,ff,5,ff,ff
  //   ,5,ff,ff,5,ff,ff,5,ff,ff,5,ff,ff,5,ff,ff,5,ff,ff,5,ff,ff,5,ff,ff
  //   ,5,ff,ff,5,ff,ff,5,ff,ff,5,ff,ff,5,ff,ff,5,ff,ff,5,ff,ff,5,ff,ff
  //   ,5,ff,ff,5,ff,ff,5,ff,ff,5,ff,ff,5,ff,ff,5,ff,ff,5,ff,ff,5,ff,ff
  //   ,5,ff,ff,5,ff,ff,5,ff,ff,5,ff,ff,5,ff,ff,5,ff,ff,5,ff,ff,5,ff,ff
  //   ,5,ff,ff,5,ff,ff,5,ff,ff,5,ff,ff,5,ff,ff,5,ff,ff,5,ff,ff,5,ff,ff
  //   ,5,ff,ff,5,ff,ff,5,ff,ff,5,ff,ff,5,ff,ff,5,ff,ff,5,ff,ff,5,ff,ff
  //   ,5,ff,ff,5,ff,ff,5,ff,ff,5,ff,ff,5,ff,ff,5,ff,ff,5,ff,ff,5,ff,ff
  //   ,5,ff,ff,5,ff,ff,5,ff,ff,5,ff,ff,5,ff,ff,5,ff,ff,5,ff,ff,5,ff,ff
  //   ,5,ff,ff,5,ff,ff,5,ff,ff,5,ff,ff,5,ff,ff,5,ff,ff,5,ff,ff,5,ff,ff
  //   ,5,ff,ff,5,ff,ff,5,ff,ff,5,ff,ff,5,ff,ff,5,ff,ff,5,ff,ff,5,ff,ff
  //   ,5,ff,ff,5,ff,ff,5,ff,ff,5,ff,ff,5,ff,ff,5,ff,ff,5,ff,ff,5,ff,ff
  //   ,5,ff,ff,5,ff,ff,5,ff,ff,5,ff,ff,5,ff,ff,5,ff,ff,5,ff,ff,5,ff,ff
  //   ,5,ff,ff,5,ff,ff,5,ff,ff,5,ff,ff,5,ff,ff,5,ff,ff,5,ff,ff,5,ff,ff
  //   ,5,ff,ff,5,ff,ff,5,ff,ff,5,ff,ff,5,ff,ff,5,ff,ff,5,ff,ff,5,ff,ff
  //   ,5,ff,ff,5,ff,ff,5,ff,ff,5,ff,ff,5,ff,ff,5,ff,ff,5,ff,ff,5,ff,ff
  //   ,5,ff,ff,5,ff,ff,5,ff,ff,5,ff,ff,5,ff,ff,5,ff,ff,5,ff,ff,5,ff,ff
  //   ,5,ff,ff,5,ff,ff,5,ff,ff,5,ff,ff,5,ff,ff,5,ff,ff,5,ff,ff,5,ff,ff
  //   ,5,ff,ff,5,ff,ff,5,ff,ff,5,ff,ff,5,ff,ff,5,ff,ff,5,ff,ff,5,ff,ff
  //   ,5,ff,ff,5,ff,ff,5,ff,ff,5,ff,ff,5,ff,ff,5,ff,ff,5,ff,ff,5,ff,ff
  //   ,5,ff,ff,5,ff,ff,5,ff,ff,5,ff,ff,5,ff,ff,5,ff,ff,5,ff,ff,5,ff,ff
  //   ,5,ff,ff,5,ff,ff,5,ff,ff,5,ff,ff,5,ff,ff,5,ff,ff,5,ff,ff,5,ff,ff
  //   ,5,ff,ff,5,ff,ff,5,ff,ff,5,ff,ff,5,ff,ff,5,ff,ff,5,ff,ff,5,ff,ff
  //   ,5,ff,ff,5,ff,ff,5,ff,ff,5,ff,ff,5,ff,ff,5,ff,ff,5,ff,ff,5,ff,ff
  //   ,5,ff,ff,5,ff,ff,5,ff,ff,5,ff,ff,5,ff,ff,5,ff,ff,5,ff,ff,5,ff,ff
  //   ,5,ff,ff,5,ff,ff,5,ff,ff,5,ff,ff,5,ff,ff,5,ff,ff,5,ff,ff,5,ff,ff
  //   ,5,ff,ff,5,ff,ff,5,ff,ff,5,ff,ff,5,ff,ff,5,ff,ff,5,ff,ff,5,ff,ff
  //   ,5,ff,ff,5,ff,ff,5,ff,ff,5,ff,ff,5,ff,ff,5,ff,ff,5,ff,ff,5,ff,ff
  //   ,5,ff,ff,5,ff,ff,5,ff,ff,5,ff,ff,5,ff,ff,5,ff,ff,5,ff,ff,5,ff,ff
  //   ,5,ff,ff,5,ff,ff,5,ff,ff,5,ff,ff,5,ff,ff,5,ff,ff,5,ff,ff,5,ff,ff
  //   ,5,ff,ff,5,ff,ff,5,ff,ff,5,ff,ff,5,ff,ff,5,ff,ff,5,ff,ff,5,ff,ff
  //   ,5,ff,ff,5,ff,ff,5,ff,ff,5,ff,ff,5,ff,ff,5,ff,ff,5,ff,ff,5,ff,ff
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  //   contents of rom_6 (hex, n*v repeats v):
  //   5,ff,ff,5,ff,ff,5,ff,ff,5,ff,ff,5,ff,ff,5,ff,ff,5,ff,ff,5,ff,ff
  //   ,5,ff,ff,5,ff,ff,5,ff,ff,5,ff,ff,5,ff,ff,5,ff,ff,5,ff,ff,5,ff,ff
  //   ,5,ff,ff,5,ff,ff,5,ff,ff,5,ff,ff,5,ff,ff,5,ff,ff,5,ff,ff,5,ff,ff
  //   ,5,ff,ff,5,ff,ff,5,ff,ff,5,ff,ff,5,ff,ff,5,ff,ff,5,ff,ff,5,ff,ff
  //   ,5,ff,ff,5,ff,ff,5,ff,ff,5,ff,ff,5,ff,ff,5,ff,ff,5,ff,ff,5,ff,ff
  //   ,5,ff,ff,5,ff,ff,5,ff,ff,5,ff,ff,5,ff,ff,5,ff,ff,5,ff,ff,5,ff,ff
  //   ,5,ff,ff,5,ff,ff,5,ff,ff,5,ff,ff,5,ff,ff,5,ff,ff,5,ff,ff,5,ff,ff
  //   ,5,ff,ff,5,ff,ff,5,ff,ff,5,ff,ff,5,ff,ff,5,ff,ff,5,ff,ff,5,ff,ff
  //   ,5,ff,ff,5,ff,ff,5,ff,ff,5,ff,ff,5,ff,ff,5,ff,ff,5,ff,ff,5,ff,ff
  //   ,5,ff,ff,5,ff,ff,5,ff,ff,5,ff,ff,5,ff,ff,5,ff,ff,5,ff,ff,5,ff,ff
  //   ,5,ff,ff,5,ff,ff,5,ff,ff,5,ff,ff,5,ff,ff,5,ff,ff,5,ff,ff,5,ff,ff
  //   ,5,ff,ff,5,ff,ff,5,ff,ff,5,ff,ff,5,ff,ff,5,ff,ff,5,ff,ff,5,ff,ff
  //   ,5,ff,ff,5,ff,ff,5,ff,ff,5,ff,ff,5,ff,ff,5,ff,ff,5,ff,ff,5,ff,ff
  //   ,5,ff,ff,5,ff,ff,5,ff,ff,5,ff,ff,5,ff,ff,5,ff,ff,5,ff,ff,5,ff,ff
  //   ,5,ff,ff,5,ff,ff,5,ff,ff,5,ff,ff,5,ff,ff,5,ff,ff,5,ff,ff,5,ff,ff
  //   ,5,ff,ff,5,ff,ff,5,ff,ff,5,ff,ff,5,ff,ff,5,ff,ff,5,ff,ff,5,ff,ff
  //   ,5,ff,ff,5,ff,ff,5,ff,ff,5,ff,ff,5,ff,ff,5,ff,ff,5,ff,ff,5,ff,ff
  //   ,5,ff,ff,5,ff,ff,5,ff,ff,5,ff,ff,5,ff,ff,5,ff,ff,5,ff,ff,5,ff,ff
  //   ,5,ff,ff,5,ff,ff,5,ff,ff,5,ff,ff,5,ff,ff,5,ff,ff,5,ff,ff,5,ff,ff
  //   ,5,ff,ff,5,ff,ff,5,ff,ff,5,ff,ff,5,ff,ff,5,ff,ff,5,ff,ff,5,ff,ff
  //   ,5,ff,ff,5,ff,ff,5,ff,ff,5,ff,ff,5,ff,ff,5,ff,ff,5,ff,ff,5,ff,ff
  //   ,5,ff,ff,5,ff,ff,5,ff,ff,5,ff,ff,5,ff,ff,5,ff,ff,5,ff,ff,5,ff,ff
  //   ,5,ff,ff,5,ff,ff,5,ff,ff,5,ff,ff,5,ff,ff,5,ff,ff,5,ff,ff,5,ff,ff
  //   ,5,ff,ff,5,ff,ff,5,ff,ff,5,ff,ff,5,ff,ff,5,ff,ff,5,ff,ff,5,ff,ff
  //   ,5,ff,ff,5,ff,ff,5,ff,ff,5,ff,ff,5,ff,ff,5,ff,ff,5,ff,ff,5,ff,ff
  //   ,5,ff,ff,5,ff,ff,5,ff,ff,5,ff,ff,5,ff,ff,5,ff,ff,5,ff,ff,5,ff,ff
  //   ,5,ff,ff,5,ff,ff,5,ff,ff,5,ff,ff,5,ff,ff,5,ff,ff,5,ff,ff,5,ff,ff
  //   ,5,ff,ff,5,ff,ff,5,ff,ff,5,ff,ff,5,ff,ff,5,ff,ff,5,ff,ff,5,ff,ff
  //   ,5,ff,ff,5,ff,ff,5,ff,ff,5,ff,ff,5,ff,ff,5,ff,ff,5,ff,ff,5,ff,ff
  //   ,5,ff,ff,5,ff,ff,5,ff,ff,5,ff,ff,5,ff,ff,5,ff,ff,5,ff,ff,5,ff,ff
  //   ,5,ff,ff,5,ff,ff,5,ff,ff,5,ff,ff,5,ff,ff,5,ff,ff,5,ff,ff,5,ff,ff
  //   ,5,ff,ff,5,ff,ff,5,ff,ff,5,ff,ff,5,ff,ff,5,ff,ff,5,ff,ff,5,ff,ff
  //   ,5,ff,ff,5,ff,ff,5,ff,ff,5,ff,ff,5,ff,ff,5,ff,ff,5,ff,ff,5,ff,ff
  //   ,5,ff,ff,5,ff,ff,5,ff,ff,5,ff,ff,5,ff,ff,5,ff,ff,5,ff,ff,5,ff,ff
  //   ,5,ff,ff,5,ff,ff,5,ff,ff,5,ff,ff,5,ff,ff,5,ff,ff,5,ff,ff,5,ff,ff
  //   ,5,ff,ff,5,ff,ff,5,ff,ff,5,ff,ff,5,ff,ff,5,ff,ff,5,ff,ff,5,ff,ff
  //   ,5,ff,ff,5,ff,ff,5,ff,ff,5,ff,ff,5,ff,ff,5,ff,ff,5,ff,ff,5,ff,ff
  //   ,5,ff,ff,5,ff,ff,5,ff,ff,5,ff,ff,5,ff,ff,5,ff,ff,5,ff,ff,5,ff,ff
  //   ,5,ff,ff,5,ff,ff,5,ff,ff,5,ff,ff,5,ff,ff,5,ff,ff,5,ff,ff,5,ff,ff
  //   ,5,ff,ff,5,ff,ff,5,ff,ff,5,ff,ff,5,ff,ff,5,ff,ff,5,ff,ff,5,ff,ff
  //   ,5,ff,ff,5,ff,ff,5,ff,ff,5,ff,ff,5,ff,ff,5,ff,ff,5,ff,ff,5,ff,ff
  //   ,5,ff,ff,5,ff,ff,5,ff,ff,5,ff,ff,5,ff,ff,5,ff,ff,5,ff,ff,5,ff,ff
  //   ,5,ff,ff,5,ff,ff,5,ff,ff,5,ff,ff,5,ff,ff,5,ff,ff,5,ff,ff,5,ff,ff
  //   ,5,ff,ff,5,ff,ff,5,ff,ff,5,ff,ff,5,ff,ff,5,ff,ff,5,ff,ff,5,ff,ff
  //   ,5,ff,ff,5,ff,ff,5,ff,ff,5,ff,ff,5,ff,ff,5,ff,ff,5,ff,ff,5,ff,ff
  //   ,5,ff,ff,5,ff,ff,5,ff,ff,5,ff,ff,5,ff,ff,5,ff,ff,5,ff,ff,5,ff,ff
  //   ,5,ff,ff,5,ff,ff,5,ff,ff,5,ff,ff,5,ff,ff,5,ff,ff,5,ff,ff,5,ff,ff
  //   ,5,ff,ff,5,ff,ff,5,ff,ff,5,ff,ff,5,ff,ff,5,ff,ff,5,ff,ff,5,ff,ff
  //   ,5,ff,ff,5,ff,ff,5,ff,ff,5,ff,ff,5,ff,ff,5,ff,ff,5,ff,ff,5,ff,ff
  //   ,5,ff,ff,5,ff,ff,5,ff,ff,5,ff,ff,5,ff,ff,5,ff,ff,5,ff,ff,5,ff,ff
  //   ,5,ff,ff,5,ff,ff,5,ff,ff,5,ff,ff,5,ff,ff,5,ff,ff,5,ff,ff,5,ff,ff
  //   ,5,ff,ff,5,ff,ff,5,ff,ff,5,ff,ff,5,ff,ff,5,ff,ff,5,ff,ff,5,ff,ff
  //   ,5,ff,ff,5,ff,ff,5,ff,ff,5,ff,ff,5,ff,ff,5,ff,ff,5,ff,ff,5,ff,ff
  //   ,5,ff,ff,5,ff,ff,5,ff,ff,5,ff,ff,5,ff,ff,5,ff,ff,5,ff,ff,5,ff,ff
  //   ,5,ff,ff,5,ff,ff,5,ff,ff,5,ff,ff,5,ff,ff,5,ff,ff,5,ff,ff,5,ff,ff
  //   ,5,ff,ff,5,ff,ff,5,ff,ff,5,ff,ff,5,ff,ff,5,ff,ff,5,ff,ff,5,ff,ff
  //   ,5,ff,ff,5,ff,ff,5,ff,ff,5,ff,ff,5,ff,ff,5,ff,ff,5,ff,ff,5,ff,ff
  //   ,5,ff,ff,5,ff,ff,5,ff,ff,5,ff,ff,5,ff,ff,5,ff,ff,5,ff,ff,5,ff,ff
  //   ,5,ff,ff,5,ff,ff,5,ff,ff,5,ff,ff,5,ff,ff,5,ff,ff,5,ff,ff,5,ff,ff
  //   ,5,ff,ff,5,ff,ff,5,ff,ff,5,ff,ff,5,ff,ff,5,ff,ff,5,ff,ff,5,ff,ff
  //   ,5,ff,ff,5,ff,ff,5,ff,ff,5,ff,ff,5,ff,ff,5,ff,ff,5,ff,ff,5,ff,ff
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  //   contents of rom_7 (hex, n*v repeats v):
  //   4098*0,200,2480,200,2500,2401,200000,251*0,200,2480,200,2500,2401
  //   ,200000,250*0,200,2480,200,2500,2401,200000,506*0,200,2480,200
  //   ,2500,2401,200000,1018*0,200,2480,200,2500,2401,200000,2041*0
  //   ,200,2480,200,2500,4004,200000,251*0,200,2480,200,2500,4004,200000
  //   ,250*0,200,2480,200,2500,4004,200000,506*0,200,2480,200,2500,4004
  //   ,200000,1018*0,200,2480,200,2500,4004,200000,2041*0,200,2480,200
  //   ,2500,2001,200000,251*0,200,2480,200,2500,2001,200000,250*0,200
  //   ,2480,200,2500,2001,200000,506*0,200,2480,200,2500,2001,200000
  //   ,1018*0,200,2480,200,2500,2001,200000,2041*0,6,200000,255*0,6
  //   ,200000,254*0,6,200000,510*0,6,200000,1022*0,6,200000,2045*0,200
  //   ,2480,200,2500,400000,200000,251*0,200,2480,200,2500,400000,200000
  //   ,250*0,200,2480,200,2500,400000,200000,506*0,200,2480,200,2500
  //   ,400000,200000,1018*0,200,2480,200,2500,400000,200000,2041*0,21
  //   ,200000,255*0,21,200000,254*0,21,200000,510*0,21,200000,1022*0
  //   ,21,200000,2045*0,11,200000,255*0,11,200000,254*0,11,200000,510*0
  //   ,11,200000,1022*0,11,200000,2045*0,51,200000,255*0,51,200000,254*0
  //   ,51,200000,510*0,51,200000,1022*0,51,200000,2045*0,200,2480,200
  //   ,2500,800,200000,251*0,200,2480,200,2500,800,200000,250*0,200
  //   ,2480,200,2500,800,200000,506*0,200,2480,200,2500,800,200000,1018*0
  //   ,200,2480,200,2500,800,200000,2041*0,18400,400,200000,253*0,18400
  //   ,400,200000,253*0,18400,400,200000,509*0,18400,400,200000,1021*0
  //   ,18000,200,2046*0,18400,400,200000,253*0,18400,400,200000,253*0
  //   ,18400,400,200000,509*0,18000,200,1022*0,18400,400,200000,2045*0
  //   ,18400,400,200000,253*0,18000,200,254*0,18400,400,200000,509*0
  //   ,18400,400,200000,1021*0,18400,400,200000,2045*0,18400,400,200000
  //   ,253*0,18400,400,200000,253*0,18000,200,510*0,18400,400,200000
  //   ,1021*0,18400,400,200000,2045*0,100004,200000,255*0,100004,200000
  //   ,254*0,100004,200000,510*0,100004,200000,1022*0,100004,200000
  //   ,2045*0,40000,200000,255*0,40000,200000,254*0,40000,200000,510*0
  //   ,40000,200000,1022*0,40000,200000
endmodule
