// Digital circuit YU1v2.dig as structural Verilog
module YU1v2 (
  input  clk,
  output [7:0] out_2,
  output [3:0] out_3,
  output [15:0] out_4,
  output [7:0] out_5,
  output [7:0] out_6,
  output [7:0] out_7,
  output [7:0] out_8,
  output [7:0] out_9,
  output [15:0] out_10,
  output [7:0] out_11,
  output [3:0] out_12,
  output [7:0] out_13
);

  wire add_1_c_o, ADO, AI, and_18_out, and_19_out, AO, BI, BO, CARO, CI, CLK_t, CLR, CO, CO1, CO2, COE, COE1,
       COE2, counter_1_ovf, counter_2_ovf, decoder_1_out_2, decoder_1_out_3, decoder_1_out_4,
       decoder_1_out_5, decoder_1_out_6, decoder_1_out_7, decoder_1_out_8, decoder_1_out_9, decoder_1_out_10,
       decoder_1_out_11, decoder_1_out_12, decoder_1_out_13, decoder_1_out_14, decoder_1_out_15, FI, HBI,
       HLT, IRI, IRI2, LBI, MAR, MI, MRI, MRI2, nor_1_out, NXT, or_1_out, or_2_out, OUT, pulldown_2_out,
       pullup_2_out, pullup_3_out, RAI, RAO, RAO2, rs_ff_as_1_q, SAO, SUB;
  wire [1:0] comparator_1_lt, driver_6_out, driver_8_out;
  wire [3:0] counter_1_out;
  wire [7:0] pulldown_4_out, xor_1_out;
  wire [7:4] register_5_q;
  wire [11:0] CW;
  wire [15:0] and_1_out, and_2_out, and_3_out, and_4_out, and_5_out, and_6_out, and_7_out, and_8_out,
       and_9_out, and_10_out, and_11_out, and_12_out, and_13_out, and_14_out, and_15_out, and_16_out,
       demultiplexer_1_out_0, demultiplexer_1_out_1, demultiplexer_1_out_2, demultiplexer_1_out_3,
       demultiplexer_1_out_4, demultiplexer_1_out_5, demultiplexer_1_out_6, demultiplexer_1_out_7,
       demultiplexer_1_out_8, demultiplexer_1_out_9, demultiplexer_1_out_10, demultiplexer_1_out_11,
       demultiplexer_1_out_12, demultiplexer_1_out_13, demultiplexer_1_out_14, demultiplexer_1_out_15,
       driver_1_out, driverinvsel_1_out, pullup_1_out;

  Counter #(.Bits(4)) counter_1 (.en(MI), .C(CLK_t), .clr(or_1_out), .out(counter_1_out), .ovf(counter_1_ovf));
  or or_1 (or_1_out, MAR, counter_1_ovf);
  assign and_1_out = demultiplexer_1_out_3 & driver_1_out;  // And and_1, 16 bits wide
  assign and_2_out = demultiplexer_1_out_2 & driver_1_out;  // And and_2, 16 bits wide
  assign and_3_out = demultiplexer_1_out_1 & driver_1_out;  // And and_3, 16 bits wide
  assign and_4_out = demultiplexer_1_out_0 & driver_1_out;  // And and_4, 16 bits wide
  Demultiplexer #(.Selector_Bits(4), .Bits(16)) demultiplexer_1 (
    .sel(counter_1_out), .in(pullup_1_out), .out_0(demultiplexer_1_out_0), .out_1(demultiplexer_1_out_1),
    .out_2(demultiplexer_1_out_2), .out_3(demultiplexer_1_out_3), .out_4(demultiplexer_1_out_4),
    .out_5(demultiplexer_1_out_5), .out_6(demultiplexer_1_out_6), .out_7(demultiplexer_1_out_7),
    .out_8(demultiplexer_1_out_8), .out_9(demultiplexer_1_out_9), .out_10(demultiplexer_1_out_10),
    .out_11(demultiplexer_1_out_11), .out_12(demultiplexer_1_out_12), .out_13(demultiplexer_1_out_13),
    .out_14(demultiplexer_1_out_14), .out_15(demultiplexer_1_out_15));
  LED led_1 (.in(and_4_out[0]));
  LED led_2 (.in(and_4_out[1]));
  LED led_3 (.in(and_4_out[2]));
  LED led_4 (.in(and_4_out[3]));
  LED led_5 (.in(and_4_out[4]));
  LED led_6 (.in(and_4_out[5]));
  LED led_7 (.in(and_4_out[6]));
  LED led_8 (.in(and_4_out[7]));
  LED led_9 (.in(and_4_out[8]));
  LED led_10 (.in(and_4_out[9]));
  LED led_11 (.in(and_4_out[10]));
  LED led_12 (.in(and_4_out[11]));
  LED led_13 (.in(and_4_out[12]));
  LED led_14 (.in(and_4_out[13]));
  LED led_15 (.in(and_4_out[14]));
  LED led_16 (.in(and_4_out[15]));
  PullUp #(.Bits(16)) pullup_1 (.out(pullup_1_out));
  LED led_17 (.in(and_2_out[0]));
  LED led_18 (.in(and_3_out[0]));
  LED led_19 (.in(and_2_out[1]));
  LED led_20 (.in(and_3_out[1]));
  LED led_21 (.in(and_2_out[2]));
  LED led_22 (.in(and_3_out[2]));
  LED led_23 (.in(and_2_out[3]));
  LED led_24 (.in(and_3_out[3]));
  LED led_25 (.in(and_2_out[4]));
  LED led_26 (.in(and_3_out[4]));
  LED led_27 (.in(and_2_out[5]));
  LED led_28 (.in(and_3_out[5]));
  LED led_29 (.in(and_2_out[6]));
  LED led_30 (.in(and_3_out[6]));
  LED led_31 (.in(and_2_out[7]));
  LED led_32 (.in(and_3_out[7]));
  LED led_33 (.in(and_2_out[8]));
  LED led_34 (.in(and_3_out[8]));
  LED led_35 (.in(and_2_out[9]));
  LED led_36 (.in(and_3_out[9]));
  LED led_37 (.in(and_2_out[10]));
  LED led_38 (.in(and_3_out[10]));
  LED led_39 (.in(and_2_out[11]));
  LED led_40 (.in(and_3_out[11]));
  LED led_41 (.in(and_2_out[12]));
  LED led_42 (.in(and_3_out[12]));
  LED led_43 (.in(and_2_out[13]));
  LED led_44 (.in(and_3_out[13]));
  LED led_45 (.in(and_2_out[14]));
  LED led_46 (.in(and_3_out[14]));
  LED led_47 (.in(and_2_out[15]));
  LED led_48 (.in(and_3_out[15]));
  assign and_5_out = demultiplexer_1_out_7 & driver_1_out;  // And and_5, 16 bits wide
  assign and_6_out = demultiplexer_1_out_6 & driver_1_out;  // And and_6, 16 bits wide
  assign and_7_out = demultiplexer_1_out_5 & driver_1_out;  // And and_7, 16 bits wide
  assign and_8_out = demultiplexer_1_out_4 & driver_1_out;  // And and_8, 16 bits wide
  LED led_49 (.in(and_8_out[0]));
  LED led_50 (.in(and_1_out[0]));
  LED led_51 (.in(and_8_out[1]));
  LED led_52 (.in(and_1_out[1]));
  LED led_53 (.in(and_8_out[2]));
  LED led_54 (.in(and_1_out[2]));
  LED led_55 (.in(and_8_out[3]));
  LED led_56 (.in(and_1_out[3]));
  LED led_57 (.in(and_8_out[4]));
  LED led_58 (.in(and_1_out[4]));
  LED led_59 (.in(and_8_out[5]));
  LED led_60 (.in(and_1_out[5]));
  LED led_61 (.in(and_8_out[6]));
  LED led_62 (.in(and_1_out[6]));
  LED led_63 (.in(and_8_out[7]));
  LED led_64 (.in(and_1_out[7]));
  LED led_65 (.in(and_8_out[8]));
  LED led_66 (.in(and_1_out[8]));
  LED led_67 (.in(and_8_out[9]));
  LED led_68 (.in(and_1_out[9]));
  LED led_69 (.in(and_8_out[10]));
  LED led_70 (.in(and_1_out[10]));
  LED led_71 (.in(and_8_out[11]));
  LED led_72 (.in(and_1_out[11]));
  LED led_73 (.in(and_8_out[12]));
  LED led_74 (.in(and_1_out[12]));
  LED led_75 (.in(and_8_out[13]));
  LED led_76 (.in(and_1_out[13]));
  LED led_77 (.in(and_8_out[14]));
  LED led_78 (.in(and_1_out[14]));
  LED led_79 (.in(and_8_out[15]));
  LED led_80 (.in(and_1_out[15]));
  LED led_81 (.in(and_6_out[0]));
  LED led_82 (.in(and_7_out[0]));
  LED led_83 (.in(and_6_out[1]));
  LED led_84 (.in(and_7_out[1]));
  LED led_85 (.in(and_6_out[2]));
  LED led_86 (.in(and_7_out[2]));
  LED led_87 (.in(and_6_out[3]));
  LED led_88 (.in(and_7_out[3]));
  LED led_89 (.in(and_6_out[4]));
  LED led_90 (.in(and_7_out[4]));
  LED led_91 (.in(and_6_out[5]));
  LED led_92 (.in(and_7_out[5]));
  LED led_93 (.in(and_6_out[6]));
  LED led_94 (.in(and_7_out[6]));
  LED led_95 (.in(and_6_out[7]));
  LED led_96 (.in(and_7_out[7]));
  LED led_97 (.in(and_6_out[8]));
  LED led_98 (.in(and_7_out[8]));
  LED led_99 (.in(and_6_out[9]));
  LED led_100 (.in(and_7_out[9]));
  LED led_101 (.in(and_6_out[10]));
  LED led_102 (.in(and_7_out[10]));
  LED led_103 (.in(and_6_out[11]));
  LED led_104 (.in(and_7_out[11]));
  LED led_105 (.in(and_6_out[12]));
  LED led_106 (.in(and_7_out[12]));
  LED led_107 (.in(and_6_out[13]));
  LED led_108 (.in(and_7_out[13]));
  LED led_109 (.in(and_6_out[14]));
  LED led_110 (.in(and_7_out[14]));
  LED led_111 (.in(and_6_out[15]));
  LED led_112 (.in(and_7_out[15]));
  LED led_113 (.in(and_12_out[0]));
  LED led_114 (.in(and_5_out[0]));
  LED led_115 (.in(and_12_out[1]));
  LED led_116 (.in(and_5_out[1]));
  LED led_117 (.in(and_12_out[2]));
  LED led_118 (.in(and_5_out[2]));
  LED led_119 (.in(and_12_out[3]));
  LED led_120 (.in(and_5_out[3]));
  LED led_121 (.in(and_12_out[4]));
  LED led_122 (.in(and_5_out[4]));
  LED led_123 (.in(and_12_out[5]));
  LED led_124 (.in(and_5_out[5]));
  LED led_125 (.in(and_12_out[6]));
  LED led_126 (.in(and_5_out[6]));
  LED led_127 (.in(and_12_out[7]));
  LED led_128 (.in(and_5_out[7]));
  LED led_129 (.in(and_12_out[8]));
  LED led_130 (.in(and_5_out[8]));
  LED led_131 (.in(and_12_out[9]));
  LED led_132 (.in(and_5_out[9]));
  LED led_133 (.in(and_12_out[10]));
  LED led_134 (.in(and_5_out[10]));
  LED led_135 (.in(and_12_out[11]));
  LED led_136 (.in(and_5_out[11]));
  LED led_137 (.in(and_12_out[12]));
  LED led_138 (.in(and_5_out[12]));
  LED led_139 (.in(and_12_out[13]));
  LED led_140 (.in(and_5_out[13]));
  LED led_141 (.in(and_12_out[14]));
  LED led_142 (.in(and_5_out[14]));
  LED led_143 (.in(and_12_out[15]));
  LED led_144 (.in(and_5_out[15]));
  assign and_9_out = demultiplexer_1_out_11 & driver_1_out;  // And and_9, 16 bits wide
  assign and_10_out = demultiplexer_1_out_10 & driver_1_out;  // And and_10, 16 bits wide
  assign and_11_out = demultiplexer_1_out_9 & driver_1_out;  // And and_11, 16 bits wide
  assign and_12_out = demultiplexer_1_out_8 & driver_1_out;  // And and_12, 16 bits wide
  LED led_145 (.in(and_10_out[0]));
  LED led_146 (.in(and_11_out[0]));
  LED led_147 (.in(and_10_out[1]));
  LED led_148 (.in(and_11_out[1]));
  LED led_149 (.in(and_10_out[2]));
  LED led_150 (.in(and_11_out[2]));
  LED led_151 (.in(and_10_out[3]));
  LED led_152 (.in(and_11_out[3]));
  LED led_153 (.in(and_10_out[4]));
  LED led_154 (.in(and_11_out[4]));
  LED led_155 (.in(and_10_out[5]));
  LED led_156 (.in(and_11_out[5]));
  LED led_157 (.in(and_10_out[6]));
  LED led_158 (.in(and_11_out[6]));
  LED led_159 (.in(and_10_out[7]));
  LED led_160 (.in(and_11_out[7]));
  LED led_161 (.in(and_10_out[8]));
  LED led_162 (.in(and_11_out[8]));
  LED led_163 (.in(and_10_out[9]));
  LED led_164 (.in(and_11_out[9]));
  LED led_165 (.in(and_10_out[10]));
  LED led_166 (.in(and_11_out[10]));
  LED led_167 (.in(and_10_out[11]));
  LED led_168 (.in(and_11_out[11]));
  LED led_169 (.in(and_10_out[12]));
  LED led_170 (.in(and_11_out[12]));
  LED led_171 (.in(and_10_out[13]));
  LED led_172 (.in(and_11_out[13]));
  LED led_173 (.in(and_10_out[14]));
  LED led_174 (.in(and_11_out[14]));
  LED led_175 (.in(and_10_out[15]));
  LED led_176 (.in(and_11_out[15]));
  LED led_177 (.in(and_16_out[0]));
  LED led_178 (.in(and_9_out[0]));
  LED led_179 (.in(and_16_out[1]));
  LED led_180 (.in(and_9_out[1]));
  LED led_181 (.in(and_16_out[2]));
  LED led_182 (.in(and_9_out[2]));
  LED led_183 (.in(and_16_out[3]));
  LED led_184 (.in(and_9_out[3]));
  LED led_185 (.in(and_16_out[4]));
  LED led_186 (.in(and_9_out[4]));
  LED led_187 (.in(and_16_out[5]));
  LED led_188 (.in(and_9_out[5]));
  LED led_189 (.in(and_16_out[6]));
  LED led_190 (.in(and_9_out[6]));
  LED led_191 (.in(and_16_out[7]));
  LED led_192 (.in(and_9_out[7]));
  LED led_193 (.in(and_16_out[8]));
  LED led_194 (.in(and_9_out[8]));
  LED led_195 (.in(and_16_out[9]));
  LED led_196 (.in(and_9_out[9]));
  LED led_197 (.in(and_16_out[10]));
  LED led_198 (.in(and_9_out[10]));
  LED led_199 (.in(and_16_out[11]));
  LED led_200 (.in(and_9_out[11]));
  LED led_201 (.in(and_16_out[12]));
  LED led_202 (.in(and_9_out[12]));
  LED led_203 (.in(and_16_out[13]));
  LED led_204 (.in(and_9_out[13]));
  LED led_205 (.in(and_16_out[14]));
  LED led_206 (.in(and_9_out[14]));
  LED led_207 (.in(and_16_out[15]));
  LED led_208 (.in(and_9_out[15]));
  LED led_209 (.in(and_14_out[0]));
  LED led_210 (.in(and_15_out[0]));
  LED led_211 (.in(and_14_out[1]));
  LED led_212 (.in(and_15_out[1]));
  LED led_213 (.in(and_14_out[2]));
  LED led_214 (.in(and_15_out[2]));
  LED led_215 (.in(and_14_out[3]));
  LED led_216 (.in(and_15_out[3]));
  LED led_217 (.in(and_14_out[4]));
  LED led_218 (.in(and_15_out[4]));
  LED led_219 (.in(and_14_out[5]));
  LED led_220 (.in(and_15_out[5]));
  LED led_221 (.in(and_14_out[6]));
  LED led_222 (.in(and_15_out[6]));
  LED led_223 (.in(and_14_out[7]));
  LED led_224 (.in(and_15_out[7]));
  LED led_225 (.in(and_14_out[8]));
  LED led_226 (.in(and_15_out[8]));
  LED led_227 (.in(and_14_out[9]));
  LED led_228 (.in(and_15_out[9]));
  LED led_229 (.in(and_14_out[10]));
  LED led_230 (.in(and_15_out[10]));
  LED led_231 (.in(and_14_out[11]));
  LED led_232 (.in(and_15_out[11]));
  LED led_233 (.in(and_14_out[12]));
  LED led_234 (.in(and_15_out[12]));
  LED led_235 (.in(and_14_out[13]));
  LED led_236 (.in(and_15_out[13]));
  LED led_237 (.in(and_14_out[14]));
  LED led_238 (.in(and_15_out[14]));
  LED led_239 (.in(and_14_out[15]));
  LED led_240 (.in(and_15_out[15]));
  assign and_13_out = demultiplexer_1_out_15 & driver_1_out;  // And and_13, 16 bits wide
  assign and_14_out = demultiplexer_1_out_14 & driver_1_out;  // And and_14, 16 bits wide
  assign and_15_out = demultiplexer_1_out_13 & driver_1_out;  // And and_15, 16 bits wide
  assign and_16_out = demultiplexer_1_out_12 & driver_1_out;  // And and_16, 16 bits wide
  LED led_241 (.in(and_13_out[0]));
  LED led_242 (.in(and_13_out[1]));
  LED led_243 (.in(and_13_out[2]));
  LED led_244 (.in(and_13_out[3]));
  LED led_245 (.in(and_13_out[4]));
  LED led_246 (.in(and_13_out[5]));
  LED led_247 (.in(and_13_out[6]));
  LED led_248 (.in(and_13_out[7]));
  LED led_249 (.in(and_13_out[8]));
  LED led_250 (.in(and_13_out[9]));
  LED led_251 (.in(and_13_out[10]));
  LED led_252 (.in(and_13_out[11]));
  LED led_253 (.in(and_13_out[12]));
  LED led_254 (.in(and_13_out[13]));
  LED led_255 (.in(and_13_out[14]));
  LED led_256 (.in(and_13_out[15]));
  assign driver_1_out = MI ? driverinvsel_1_out : 16'bz;  // Driver driver_1
  PullDown #(.Bits(16)) pulldown_1 (.out(driver_1_out));
  RS_FF_AS rs_ff_as_1 (.S(HLT), .R(CLR), .Q(rs_ff_as_1_q));  // open: nQ
  LED led_257 (.in(out_8[7]));
  LED led_258 (.in(out_7[7]));
  LED led_259 (.in(out_5[7]));
  LED led_260 (.in(out_2[7]));
  LED led_261 (.in(out_8[3]));
  LED led_262 (.in(out_8[4]));
  LED led_263 (.in(out_8[5]));
  LED led_264 (.in(out_8[6]));
  LED led_265 (.in(out_7[3]));
  LED led_266 (.in(out_7[4]));
  LED led_267 (.in(out_7[5]));
  LED led_268 (.in(out_7[6]));
  LED led_269 (.in(out_5[3]));
  LED led_270 (.in(out_5[4]));
  LED led_271 (.in(out_5[5]));
  LED led_272 (.in(out_5[6]));
  LED led_273 (.in(out_2[3]));
  LED led_274 (.in(out_2[4]));
  LED led_275 (.in(out_2[5]));
  LED led_276 (.in(out_2[6]));
  CounterPreset #(.Bits(16)) counterpreset_1 (
    .en(COE), .C(CLK_t), .dir(pulldown_2_out), .in(driverinvsel_1_out), .ld(CI), .clr(CLR), .out(out_4),
    .ovf(CLR));
  PullDown pulldown_2 (.out(pulldown_2_out));
  assign driverinvsel_1_out = ~CO ? {out_7, out_6} : 16'bz;  // DriverInvSel driverinvsel_1
  Register #(.Bits(16)) register_1 (.D(driverinvsel_1_out), .C(CLK_t), .en(MRI), .Q(out_10));
  and and_17 (CLK_t, clk, ~rs_ff_as_1_q);  // And
  LED led_277 (.in(out_8[0]));
  LED led_278 (.in(out_8[1]));
  LED led_279 (.in(out_8[2]));
  LED led_280 (.in(out_7[0]));
  LED led_281 (.in(out_7[1]));
  LED led_282 (.in(out_7[2]));
  LED led_283 (.in(out_5[0]));
  LED led_284 (.in(out_5[1]));
  LED led_285 (.in(out_5[2]));
  LED led_286 (.in(out_2[0]));
  LED led_287 (.in(out_2[1]));
  LED led_288 (.in(out_2[2]));
  assign driverinvsel_1_out = CO ? out_4 : 16'bz;  // Driver driver_2
  and and_18 (and_18_out, out_10[15], RAO);
  LED led_289 (.in(out_9[4]));
  LED led_290 (.in(out_9[5]));
  LED led_291 (.in(out_9[6]));
  LED led_292 (.in(out_9[7]));
  LED led_293 (.in(out_6[4]));
  LED led_294 (.in(out_6[5]));
  LED led_295 (.in(out_6[6]));
  LED led_296 (.in(out_6[7]));
  LED led_297 (.in(decoder_1_out_15));
  LED led_298 (.in(decoder_1_out_14));
  Register #(.Bits(8)) register_2 (.D(out_11), .C(CLK_t), .en(HBI), .Q(out_7));
  Register #(.Bits(8)) register_3 (.D(out_11), .C(CLK_t), .en(LBI), .Q(out_6));
  RAMDualPort #(.AddrBits(16), .Bits(8)) ramdualport_1 (
    .A(out_10), .Din(out_11), .str(RAI), .C(CLK_t), .ld(and_18_out), .D(out_11));
  LED led_299 (.in(out_9[0]));
  LED led_300 (.in(out_9[1]));
  LED led_301 (.in(out_9[2]));
  LED led_302 (.in(out_9[3]));
  LED led_303 (.in(out_6[0]));
  LED led_304 (.in(out_6[1]));
  LED led_305 (.in(out_6[2]));
  LED led_306 (.in(out_6[3]));
  LED led_307 (.in(out_12[0]));
  LED led_308 (.in(out_12[1]));
  LED led_309 (.in(out_12[2]));
  LED led_310 (.in(out_12[3]));
  LED led_311 (.in(out_3[0]));
  LED led_312 (.in(out_3[1]));
  LED led_313 (.in(out_3[2]));
  LED led_314 (.in(out_3[3]));
  LED led_315 (.in(decoder_1_out_13));
  LED led_316 (.in(decoder_1_out_12));
  LED led_317 (.in(decoder_1_out_11));
  LED led_318 (.in(decoder_1_out_10));
  and and_19 (and_19_out, RAO, ~out_10[15]);  // And
  ROM #(.AddrBits(16), .Bits(8)) rom_1 (.A(out_10), .sel(and_19_out), .D(out_11));
  Register #(.Bits(8)) register_4 (.D(out_11), .C(CLK_t), .en(OUT), .Q(out_13));
  LED led_319 (.in(out_4[13]));
  LED led_320 (.in(out_4[14]));
  LED led_321 (.in(out_4[15]));
  LED led_322 (.in(out_10[13]));
  LED led_323 (.in(out_10[14]));
  LED led_324 (.in(out_10[15]));
  LED led_325 (.in(decoder_1_out_9));
  LED led_326 (.in(decoder_1_out_8));
  LED led_327 (.in(decoder_1_out_7));
  LED led_328 (.in(decoder_1_out_6));
  PullDown #(.Bits(8)) pulldown_3 (.out(out_11));
  LED led_329 (.in(out_4[9]));
  LED led_330 (.in(out_4[10]));
  LED led_331 (.in(out_4[11]));
  LED led_332 (.in(out_4[12]));
  LED led_333 (.in(out_10[9]));
  LED led_334 (.in(out_10[10]));
  LED led_335 (.in(out_10[11]));
  LED led_336 (.in(out_10[12]));
  LED led_337 (.in(decoder_1_out_5));
  LED led_338 (.in(decoder_1_out_4));
  LED led_339 (.in(decoder_1_out_3));
  LED led_340 (.in(decoder_1_out_2));
  Register #(.Bits(8)) register_5 (.D(out_11), .C(CLK_t), .en(IRI), .Q({register_5_q, out_12}));
  PullDown #(.Bits(8)) pulldown_4 (.out(pulldown_4_out));
  Register #(.Bits(8)) register_6 (.D(out_11), .C(CLK_t), .en(BI), .Q(out_9));
  Register #(.Bits(8)) register_7 (.D(out_11), .C(CLK_t), .en(AI), .Q(out_8));
  assign out_11 = BO ? out_9 : 8'bz;  // Driver driver_3
  assign out_11 = AO ? out_8 : 8'bz;  // Driver driver_4
  PullDown pulldown_5 (.out(driver_6_out[1]));
  LED led_341 (.in(out_4[5]));
  LED led_342 (.in(out_4[6]));
  LED led_343 (.in(out_4[7]));
  LED led_344 (.in(out_4[8]));
  LED led_345 (.in(out_10[5]));
  LED led_346 (.in(out_10[6]));
  LED led_347 (.in(out_10[7]));
  LED led_348 (.in(out_10[8]));
  LED led_349 (.in(out_11[5]));
  LED led_350 (.in(out_11[6]));
  LED led_351 (.in(out_11[7]));
  LED led_352 (.in(out_13[5]));
  LED led_353 (.in(out_13[6]));
  LED led_354 (.in(out_13[7]));
  Decoder #(.Selector_Bits(4)) decoder_1 (
    .sel(CW[3:0]), .out_0(CO1), .out_1(COE1), .out_2(decoder_1_out_2), .out_3(decoder_1_out_3),
    .out_4(decoder_1_out_4), .out_5(decoder_1_out_5), .out_6(decoder_1_out_6), .out_7(decoder_1_out_7),
    .out_8(decoder_1_out_8), .out_9(decoder_1_out_9), .out_10(decoder_1_out_10), .out_11(decoder_1_out_11),
    .out_12(decoder_1_out_12), .out_13(decoder_1_out_13), .out_14(decoder_1_out_14), .out_15(decoder_1_out_15));
  assign pulldown_4_out = SUB ? {8{1'b1}} : 8'bz;  // Driver driver_5
  assign xor_1_out = pulldown_4_out ^ out_9;  // XOr xor_1, 8 bits wide
  LED led_355 (.in(out_4[1]));
  LED led_356 (.in(out_4[2]));
  LED led_357 (.in(out_4[3]));
  LED led_358 (.in(out_4[4]));
  LED led_359 (.in(out_10[1]));
  LED led_360 (.in(out_10[2]));
  LED led_361 (.in(out_10[3]));
  LED led_362 (.in(out_10[4]));
  LED led_363 (.in(out_11[1]));
  LED led_364 (.in(out_11[2]));
  LED led_365 (.in(out_11[3]));
  LED led_366 (.in(out_11[4]));
  LED led_367 (.in(out_13[1]));
  LED led_368 (.in(out_13[2]));
  LED led_369 (.in(out_13[3]));
  LED led_370 (.in(out_13[4]));
  Counter #(.Bits(4)) counter_2 (.en(pullup_2_out), .C(CLK_t), .clr(or_2_out), .out(CW[3:0]), .ovf(counter_2_ovf));
  PullUp pullup_2 (.out(pullup_2_out));
  Comparator #(.Bits(8)) comparator_1 (
    .a(out_8), .b(xor_1_out), .gt(comparator_1_lt[1]), .lt(comparator_1_lt[0]));  // open: eq
  assign driver_6_out = CARO ? comparator_1_lt : 2'bz;  // Driver driver_6
  PullDown pulldown_6 (.out(driver_6_out[0]));
  LED led_371 (.in(out_4[0]));
  LED led_372 (.in(out_10[0]));
  LED led_373 (.in(out_11[0]));
  LED led_374 (.in(out_13[0]));
  or or_2 (or_2_out, NXT, counter_2_ovf);
  Add #(.Bits(8)) add_1 (.a(out_8), .b(xor_1_out), .c_i(SUB), .s(out_5), .c_o(add_1_c_o));
  assign out_11 = ADO ? out_5 : 8'bz;  // Driver driver_7
  assign driver_8_out[1] = CARO ? add_1_c_o : 1'bz;  // Driver driver_8
  PullDown pulldown_7 (.out(driver_8_out[1]));
  PullDown #(.Bits(4)) pulldown_8 (.out(CW[11:8]));
  BarrelShifter #(.Bits(8)) barrelshifter_1 (.in(out_8), .shift(xor_1_out[3:0]), .out(out_2));
  assign out_11 = SAO ? out_2 : 8'bz;  // Driver driver_9
  PullDown pulldown_9 (.out(driver_8_out[0]));
  ROM #(.AddrBits(16), .Bits(24)) rom_2 (
    .A({out_12, CW[11:8], out_3, CW[3:0]}), .sel(pullup_3_out),
    .D({MAR, MI, NXT, OUT, CLR, HLT, IRI2, FI, CARO, RAI, RAO2, MRI2, CI, COE2, CO2, LBI, HBI, SUB, SAO, ADO, BO, AO, BI, AI}));
  PullUp pullup_3 (.out(pullup_3_out));
  Register #(.Bits(4)) register_8 (.D({driver_6_out, driver_8_out}), .C(CLK_t), .en(FI), .Q(out_3));
  nor nor_1 (nor_1_out, out_8[0], out_8[1], out_8[2], out_8[3], out_8[4], out_8[5], out_8[6], out_8[7]);
  assign driver_8_out[0] = CARO ? nor_1_out : 1'bz;  // Driver driver_10
  or or_3 (MRI, CO1, MRI2);
  or or_4 (CO, CO1, CO2);
  or or_5 (COE, COE1, COE2);
  or or_6 (RAO, COE1, RAO2);
  or or_7 (IRI, COE1, IRI2);

  // Other names for the same wires on the sheet: CW (some bits) = {out_12, out_3}; IRP[3:0] = out_12;
  //   ADP[7:0] = out_5; AP[7:0] = out_8; BP[7:0] = out_9; BUS[7:0] = out_11; FO[3:0] = out_3; HBP[7:0] = out_7;
  //   LBP[7:0] = out_6; MRI1 = CO1; MRP[15:0] = out_10; OUP[7:0] = out_13; PCP[15:0] = out_4; IRI1 = COE1;
  //   RAO1 = COE1; SAP[7:0] = out_2

  // Notes on the sheet:
  //   16x16 LED Matrix
  //   Graphics Logic
  //   Clock
  //   Probes
  //   CPU
  //   contents of rom_1 (hex, n*v repeats v):
  //   b,57,57,b,57,57,b,57,57,b,57,57,b,57,57,b,57,57,b,57,57,b,57,57
  //   ,b,57,57,b,57,57,b,57,57,b,57,57,b,57,57,b,57,57,b,57,57,b,57,57
  //   ,b,57,57,b,57,57,b,57,57,b,57,57,b,57,57,b,57,57,b,57,57,b,57,57
  //   ,b,57,57,b,57,57,b,57,57,b,57,57,b,57,57,b,57,57,b,57,57,b,57,57
  //   ,b,57,57,b,57,57,b,57,57,b,57,57,b,57,57,b,57,57,b,57,57,b,57,57
  //   ,b,57,57,b,57,57,b,57,57,b,57,57,b,57,57,b,57,57,b,57,57,b,57,57
  //   ,b,57,57,b,57,57,b,57,57,b,57,57,b,57,57,b,57,57,b,57,57,b,57,57
  //   ,b,57,57,b,57,57,b,57,57,b,57,57,b,57,57,b,57,57,b,57,57,b,57,57
  //   ,b,57,57,b,57,57,b,57,57,b,57,57,b,57,57,b,57,57,b,57,57,b,57,57
  //   ,b,57,57,b,57,57,b,57,57,b,57,57,b,57,57,b,57,57,b,57,57,b,57,57
  //   ,b,57,57,b,57,57,b,57,57,b,57,57,b,57,57,b,57,57,b,57,57,b,57,57
  //   ,b,57,57,b,57,57,b,57,57,b,57,57,b,57,57,b,57,57,b,57,57,b,57,57
  //   ,b,57,57,b,57,57,b,57,57,b,57,57,b,57,57,b,57,57,b,57,57,b,57,57
  //   ,b,57,57,b,57,57,b,57,57,b,57,57,b,57,57,b,57,57,b,57,57,b,57,57
  //   ,b,57,57,b,57,57,b,57,57,b,57,57,b,57,57,b,57,57,b,57,57,b,57,57
  //   ,b,57,57,b,57,57,b,57,57,b,57,57,b,57,57,b,57,57,b,57,57,b,57,57
  //   ,b,57,57,b,57,57,b,57,57,b,57,57,b,57,57,b,57,57,b,57,57,b,57,57
  //   ,b,57,57,b,57,57,b,57,57,b,57,57,b,57,57,b,57,57,b,57,57,b,57,57
  //   ,b,57,57,b,57,57,b,57,57,b,57,57,b,57,57,b,57,57,b,57,57,b,57,57
  //   ,b,57,57,b,57,57,b,57,57,b,57,57,b,57,57,b,57,57,b,57,57,b,57,57
  //   ,b,57,57,b,57,57,b,57,57,b,57,57,b,57,57,b,57,57,b,57,57,b,57,57
  //   ,b,57,57,b,57,57,b,57,57,b,57,57,b,57,57,b,57,57,b,57,57,b,57,57
  //   ,b,57,57,b,57,57,b,57,57,b,57,57,b,57,57,b,57,57,b,57,57,b,57,57
  //   ,b,57,57,b,57,57,b,57,57,b,57,57,b,57,57,b,57,57,b,57,57,b,57,57
  //   ,b,57,57,b,57,57,b,57,57,b,57,57,b,57,57,b,57,57,b,57,57,b,57,57
  //   ,b,57,57,b,57,57,b,57,57,b,57,57,b,57,57,b,57,57,b,57,57,b,57,57
  //   ,b,57,57,b,57,57,b,57,57,b,57,57,b,57,57,b,57,57,b,57,57,b,57,57
  //   ,b,57,57,b,57,57,b,57,57,b,57,57,b,57,57,b,57,57,b,57,57,b,57,57
  //   ,b,57,57,b,57,57,b,57,57,b,57,57,b,57,57,b,57,57,b,57,57,b,57,57
  //   ,b,57,57,b,57,57,b,57,57,b,57,57,b,57,57,b,57,57,b,57,57,b,57,57
  //   ,b,57,57,b,57,57,b,57,57,b,57,57,b,57,57,b,57,57,b,57,57,b,57,57
  //   ,b,57,57,b,57,57,b,57,57,b,57,57,b,57,57,b,57,57,b,57,57,b,57,57
  //   ,b,57,57,b,57,57,b,57,57,b,57,57,b,57,57,b,57,57,b,57,57,b,57,57
  //   ,b,57,57,b,57,57,b,57,57,b,57,57,b,57,57,b,57,57,b,57,57,b,57,57
  //   ,b,57,57,b,57,57,b,57,57,b,57,57,b,57,57,b,57,57,b,57,57,b,57,57
  //   ,b,57,57,b,57,57,b,57,57,b,57,57,b,57,57,b,57,57,b,57,57,b,57,57
  //   ,b,57,57,b,57,57,b,57,57,b,57,57,b,57,57,b,57,57,b,57,57,b,57,57
  //   ,b,57,57,b,57,57,b,57,57,b,57,57,b,57,57,b,57,57,b,57,57,b,57,57
  //   ,b,57,57,b,57,57,b,57,57,b,57,57,b,57,57,b,57,57,b,57,57,b,57,57
  //   ,b,57,57,b,57,57,b,57,57,b,57,57,b,57,57,b,57,57,b,57,57,b,57,57
  //   ,b,57,57,b,57,57,b,57,57,b,57,57,b,57,57,b,57,57,b,57,57,b,57,57
  //   ,b,57,57,b,57,57,b,57,57,b,57,57,b,57,57,b,57,57,b,57,57,b,57,57
  //   ,b,57,57,b,57,57,b,57,57,b,57,57,b,57,57,b,57,57,b,57,57,b,57,57
  //   ,b,57,57,b,57,57,b,57,57,b,57,57,b,57,57,b,57,57,b,57,57,b,57,57
  //   ,b,57,57,b,57,57,b,57,57,b,57,57,b,57,57,b,57,57,b,57,57,b,57,57
  //   ,b,57,57,b,57,57,b,57,57,b,57,57,b,57,57,b,57,57,b,57,57,b,57,57
  //   ,b,57,57,b,57,57,b,57,57,b,57,57,b,57,57,b,57,57,b,57,57,b,57,57
  //   ,b,57,57,b,57,57,b,57,57,b,57,57,b,57,57,b,57,57,b,57,57,b,57,57
  //   ,b,57,57,b,57,57,b,57,57,b,57,57,b,57,57,b,57,57,b,57,57,b,57,57
  //   ,b,57,57,b,57,57,b,57,57,b,57,57,b,57,57,b,57,57,b,57,57,b,57,57
  //   ,b,57,57,b,57,57,b,57,57,b,57,57,b,57,57,b,57,57,b,57,57,b,57,57
  //   ,b,57,57,b,57,57,b,57,57,b,57,57,b,57,57,b,57,57,b,57,57,b,57,57
  //   ,b,57,57,b,57,57,b,57,57,b,57,57,b,57,57,b,57,57,b,57,57,b,57,57
  //   ,b,57,57,b,57,57,b,57,57,b,57,57,b,57,57,b,57,57,b,57,57,b,57,57
  //   ,b,57,57,b,57,57,b,57,57,b,57,57,b,57,57,b,57,57,b,57,57,b,57,57
  //   ,b,57,57,b,57,57,b,57,57,b,57,57,b,57,57,b,57,57,b,57,57,b,57,57
  //   ,b,57,57,b,57,57,b,57,57,b,57,57,b,57,57,b,57,57,b,57,57,b,57,57
  //   ,b,57,57,b,57,57,b,57,57,b,57,57,b,57,57,b,57,57,b,57,57,b,57,57
  //   ,b,57,57,b,57,57,b,57,57,b,57,57,b,57,57,b,57,57,b,57,57,b,57,57
  //   ,b,57,57,b,57,57,b,57,57,b,57,57,b,57,57,b,57,57,b,57,57,b,57,57
  //   ,b,57,57,b,57,57,b,57,57,b,57,57,b,57,57,b,57,57,b,57,57,b,57,57
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  //   contents of rom_2 (hex, n*v repeats v):
  //   4098*0,200,2480,200,2500,2401,200000,251*0,200,2480,200,2500,2401
  //   ,200000,250*0,200,2480,200,2500,2401,200000,506*0,200,2480,200
  //   ,2500,2401,200000,1018*0,200,2480,200,2500,2401,200000,2041*0
  //   ,200,2480,200,2500,4004,200000,251*0,200,2480,200,2500,4004,200000
  //   ,250*0,200,2480,200,2500,4004,200000,506*0,200,2480,200,2500,4004
  //   ,200000,1018*0,200,2480,200,2500,4004,200000,2041*0,200,2480,200
  //   ,2500,2001,200000,251*0,200,2480,200,2500,2001,200000,250*0,200
  //   ,2480,200,2500,2001,200000,506*0,200,2480,200,2500,2001,200000
  //   ,1018*0,200,2480,200,2500,2001,200000,2041*0,6,200000,255*0,6
  //   ,200000,254*0,6,200000,510*0,6,200000,1022*0,6,200000,2045*0,200
  //   ,2480,200,2500,400000,200000,251*0,200,2480,200,2500,400000,200000
  //   ,250*0,200,2480,200,2500,400000,200000,506*0,200,2480,200,2500
  //   ,400000,200000,1018*0,200,2480,200,2500,400000,200000,2041*0,21
  //   ,200000,255*0,21,200000,254*0,21,200000,510*0,21,200000,1022*0
  //   ,21,200000,2045*0,11,200000,255*0,11,200000,254*0,11,200000,510*0
  //   ,11,200000,1022*0,11,200000,2045*0,51,200000,255*0,51,200000,254*0
  //   ,51,200000,510*0,51,200000,1022*0,51,200000,2045*0,200,2480,200
  //   ,2500,800,200000,251*0,200,2480,200,2500,800,200000,250*0,200
  //   ,2480,200,2500,800,200000,506*0,200,2480,200,2500,800,200000,1018*0
  //   ,200,2480,200,2500,800,200000,2041*0,18400,400,200000,253*0,18400
  //   ,400,200000,253*0,18400,400,200000,509*0,18400,400,200000,1021*0
  //   ,18000,200,2046*0,18400,400,200000,253*0,18400,400,200000,253*0
  //   ,18400,400,200000,509*0,18000,200,1022*0,18400,400,200000,2045*0
  //   ,18400,400,200000,253*0,18000,200,254*0,18400,400,200000,509*0
  //   ,18400,400,200000,1021*0,18400,400,200000,2045*0,18400,400,200000
  //   ,253*0,18400,400,200000,253*0,18000,200,510*0,18400,400,200000
  //   ,1021*0,18400,400,200000,2045*0,100004,200000,255*0,100004,200000
  //   ,254*0,100004,200000,510*0,100004,200000,1022*0,100004,200000
  //   ,2045*0,40000,200000,255*0,40000,200000,254*0,40000,200000,510*0
  //   ,40000,200000,1022*0,40000,200000
endmodule
